// Logisim project 74Microcircuit.circ as structural Verilog: 6 circuits, main circuit sub74HC174
module sub74HC174 (
  input  in_1,
  input  in_2,
  input  in_3,
  input  in_4,
  input  in_5,
  input  in_6,
  input  in_7,
  input  in_8,
  input  in_9,
  input  in_10,
  output out_11,
  output out_12,
  output out_13,
  output out_14,
  output out_15,
  output out_16
);

  wire and_1_out, controlled_buffer_1_out, controlled_buffer_2_out, controlled_buffer_3_out,
       controlled_buffer_5_out, controlled_buffer_7_out, controlled_buffer_9_out, controlled_buffer_10_out,
       controlled_buffer_13_out, d_ff_1_q, d_ff_2_q, d_ff_3_q, d_ff_4_q, d_ff_5_q, d_ff_6_q, not_1_out,
       not_2_out;

  not not_1 (not_1_out, in_10);
  assign controlled_buffer_1_out = and_1_out ? in_7 : 1'bz;  // Controlled_Buffer controlled_buffer_1
  assign controlled_buffer_2_out = and_1_out ? in_8 : 1'bz;  // Controlled_Buffer controlled_buffer_2
  and and_1 (and_1_out, in_9, not_1_out);
  assign controlled_buffer_3_out = and_1_out ? in_1 : 1'bz;  // Controlled_Buffer controlled_buffer_3
  not not_2 (not_2_out, controlled_buffer_1_out);
  D_Flip_Flop d_ff_1 (
    .D(controlled_buffer_3_out), .clk(controlled_buffer_2_out), .Q(d_ff_1_q), .reset(not_2_out));  // open: Qn, preset
  assign out_11 = and_1_out ? d_ff_1_q : 1'bz;  // Controlled_Buffer controlled_buffer_4
  assign controlled_buffer_5_out = and_1_out ? in_2 : 1'bz;  // Controlled_Buffer controlled_buffer_5
  D_Flip_Flop d_ff_2 (
    .D(controlled_buffer_5_out), .clk(controlled_buffer_2_out), .Q(d_ff_2_q), .reset(not_2_out));  // open: Qn, preset
  assign out_12 = and_1_out ? d_ff_2_q : 1'bz;  // Controlled_Buffer controlled_buffer_6
  assign controlled_buffer_7_out = and_1_out ? in_3 : 1'bz;  // Controlled_Buffer controlled_buffer_7
  D_Flip_Flop d_ff_3 (
    .D(controlled_buffer_7_out), .clk(controlled_buffer_2_out), .Q(d_ff_3_q), .reset(not_2_out));  // open: Qn, preset
  assign out_13 = and_1_out ? d_ff_3_q : 1'bz;  // Controlled_Buffer controlled_buffer_8
  assign controlled_buffer_9_out = and_1_out ? in_4 : 1'bz;  // Controlled_Buffer controlled_buffer_9
  D_Flip_Flop d_ff_4 (
    .D(controlled_buffer_9_out), .clk(controlled_buffer_2_out), .Q(d_ff_4_q), .reset(not_2_out));  // open: Qn, preset
  assign controlled_buffer_10_out = and_1_out ? in_5 : 1'bz;  // Controlled_Buffer controlled_buffer_10
  assign out_14 = and_1_out ? d_ff_4_q : 1'bz;  // Controlled_Buffer controlled_buffer_11
  D_Flip_Flop d_ff_5 (
    .D(controlled_buffer_10_out), .clk(controlled_buffer_2_out), .Q(d_ff_5_q), .reset(not_2_out));  // open: Qn, preset
  assign out_15 = and_1_out ? d_ff_5_q : 1'bz;  // Controlled_Buffer controlled_buffer_12
  assign controlled_buffer_13_out = and_1_out ? in_6 : 1'bz;  // Controlled_Buffer controlled_buffer_13
  D_Flip_Flop d_ff_6 (
    .D(controlled_buffer_13_out), .clk(controlled_buffer_2_out), .Q(d_ff_6_q), .reset(not_2_out));  // open: Qn, preset
  assign out_16 = and_1_out ? d_ff_6_q : 1'bz;  // Controlled_Buffer controlled_buffer_14
endmodule

module sub74HC574 (
  input  in_1,
  input  in_2,
  input  in_3,
  input  in_4,
  input  in_5,
  input  in_6,
  input  in_7,
  input  in_8,
  input  in_9,
  input  in_10,
  input  in_11,
  input  in_12,
  output out_13,
  output out_14,
  output out_15,
  output out_16,
  output out_17,
  output out_18,
  output out_19,
  output out_20
);

  wire and_1_out, controlled_buffer_1_out, controlled_buffer_2_out, controlled_buffer_3_out,
       controlled_buffer_4_out, controlled_buffer_6_out, controlled_buffer_7_out, controlled_buffer_8_out,
       controlled_buffer_10_out, controlled_buffer_12_out, controlled_buffer_13_out,
       controlled_buffer_14_out, controlled_buffer_16_out, controlled_buffer_18_out,
       controlled_buffer_19_out, controlled_buffer_20_out, controlled_buffer_22_out,
       controlled_buffer_24_out, controlled_buffer_25_out, d_ff_1_q, d_ff_2_q, d_ff_3_q, d_ff_4_q, d_ff_5_q,
       d_ff_6_q, d_ff_7_q, d_ff_8_q, not_1_out, not_2_out;

  not not_1 (not_1_out, in_12);
  assign controlled_buffer_1_out = and_1_out ? in_9 : 1'bz;  // Controlled_Buffer controlled_buffer_1
  assign controlled_buffer_2_out = and_1_out ? in_10 : 1'bz;  // Controlled_Buffer controlled_buffer_2
  and and_1 (and_1_out, in_11, not_1_out);
  assign controlled_buffer_3_out = and_1_out ? in_1 : 1'bz;  // Controlled_Buffer controlled_buffer_3
  D_Flip_Flop d_ff_1 (
    .D(controlled_buffer_3_out), .clk(controlled_buffer_1_out), .Q(d_ff_1_q));  // open: Qn, preset, reset
  not not_2 (not_2_out, controlled_buffer_2_out);
  assign controlled_buffer_4_out = and_1_out ? d_ff_1_q : 1'bz;  // Controlled_Buffer controlled_buffer_4
  assign out_13 = not_2_out ? controlled_buffer_4_out : 1'bz;  // Controlled_Buffer controlled_buffer_5
  assign controlled_buffer_6_out = and_1_out ? in_2 : 1'bz;  // Controlled_Buffer controlled_buffer_6
  D_Flip_Flop d_ff_2 (
    .D(controlled_buffer_6_out), .clk(controlled_buffer_1_out), .Q(d_ff_2_q));  // open: Qn, preset, reset
  assign controlled_buffer_7_out = and_1_out ? in_3 : 1'bz;  // Controlled_Buffer controlled_buffer_7
  D_Flip_Flop d_ff_3 (
    .D(controlled_buffer_7_out), .clk(controlled_buffer_1_out), .Q(d_ff_3_q));  // open: Qn, preset, reset
  assign controlled_buffer_8_out = and_1_out ? d_ff_2_q : 1'bz;  // Controlled_Buffer controlled_buffer_8
  assign out_14 = not_2_out ? controlled_buffer_8_out : 1'bz;  // Controlled_Buffer controlled_buffer_9
  assign controlled_buffer_10_out = and_1_out ? d_ff_3_q : 1'bz;  // Controlled_Buffer controlled_buffer_10
  assign out_15 = not_2_out ? controlled_buffer_10_out : 1'bz;  // Controlled_Buffer controlled_buffer_11
  assign controlled_buffer_12_out = and_1_out ? in_4 : 1'bz;  // Controlled_Buffer controlled_buffer_12
  D_Flip_Flop d_ff_4 (
    .D(controlled_buffer_12_out), .clk(controlled_buffer_1_out), .Q(d_ff_4_q));  // open: Qn, preset, reset
  assign controlled_buffer_13_out = and_1_out ? in_5 : 1'bz;  // Controlled_Buffer controlled_buffer_13
  D_Flip_Flop d_ff_5 (
    .D(controlled_buffer_13_out), .clk(controlled_buffer_1_out), .Q(d_ff_5_q));  // open: Qn, preset, reset
  assign controlled_buffer_14_out = and_1_out ? d_ff_4_q : 1'bz;  // Controlled_Buffer controlled_buffer_14
  assign out_16 = not_2_out ? controlled_buffer_14_out : 1'bz;  // Controlled_Buffer controlled_buffer_15
  assign controlled_buffer_16_out = and_1_out ? d_ff_5_q : 1'bz;  // Controlled_Buffer controlled_buffer_16
  assign out_17 = not_2_out ? controlled_buffer_16_out : 1'bz;  // Controlled_Buffer controlled_buffer_17
  assign controlled_buffer_18_out = and_1_out ? in_6 : 1'bz;  // Controlled_Buffer controlled_buffer_18
  D_Flip_Flop d_ff_6 (
    .D(controlled_buffer_18_out), .clk(controlled_buffer_1_out), .Q(d_ff_6_q));  // open: Qn, preset, reset
  assign controlled_buffer_19_out = and_1_out ? in_7 : 1'bz;  // Controlled_Buffer controlled_buffer_19
  D_Flip_Flop d_ff_7 (
    .D(controlled_buffer_19_out), .clk(controlled_buffer_1_out), .Q(d_ff_7_q));  // open: Qn, preset, reset
  assign controlled_buffer_20_out = and_1_out ? d_ff_6_q : 1'bz;  // Controlled_Buffer controlled_buffer_20
  assign out_18 = not_2_out ? controlled_buffer_20_out : 1'bz;  // Controlled_Buffer controlled_buffer_21
  assign controlled_buffer_22_out = and_1_out ? d_ff_7_q : 1'bz;  // Controlled_Buffer controlled_buffer_22
  assign out_19 = not_2_out ? controlled_buffer_22_out : 1'bz;  // Controlled_Buffer controlled_buffer_23
  assign controlled_buffer_24_out = and_1_out ? in_8 : 1'bz;  // Controlled_Buffer controlled_buffer_24
  D_Flip_Flop d_ff_8 (
    .D(controlled_buffer_24_out), .clk(controlled_buffer_1_out), .Q(d_ff_8_q));  // open: Qn, preset, reset
  assign controlled_buffer_25_out = and_1_out ? d_ff_8_q : 1'bz;  // Controlled_Buffer controlled_buffer_25
  assign out_20 = not_2_out ? controlled_buffer_25_out : 1'bz;  // Controlled_Buffer controlled_buffer_26
endmodule

module sub74HC4066 (
  input  in_1,
  input  in_2,
  input  in_3,
  input  in_4,
  input  in_5,
  input  in_6,
  input  in_7,
  input  in_8,
  input  in_9,
  input  in_10,
  output out_11,
  output out_12,
  output out_13,
  output out_14
);

  wire and_1_out, controlled_buffer_1_out, controlled_buffer_2_out, controlled_buffer_3_out,
       controlled_buffer_4_out, controlled_buffer_5_out, controlled_buffer_6_out, controlled_buffer_7_out,
       controlled_buffer_8_out, not_1_out;

  assign controlled_buffer_1_out = and_1_out ? in_2 : 1'bz;  // Controlled_Buffer controlled_buffer_1
  assign controlled_buffer_2_out = and_1_out ? in_4 : 1'bz;  // Controlled_Buffer controlled_buffer_2
  assign controlled_buffer_3_out = and_1_out ? in_6 : 1'bz;  // Controlled_Buffer controlled_buffer_3
  assign controlled_buffer_4_out = and_1_out ? in_8 : 1'bz;  // Controlled_Buffer controlled_buffer_4
  not not_1 (not_1_out, in_10);
  assign controlled_buffer_5_out = controlled_buffer_1_out ? in_1 : 1'bz;  // Controlled_Buffer controlled_buffer_5
  assign controlled_buffer_6_out = controlled_buffer_2_out ? in_3 : 1'bz;  // Controlled_Buffer controlled_buffer_6
  assign controlled_buffer_7_out = controlled_buffer_3_out ? in_5 : 1'bz;  // Controlled_Buffer controlled_buffer_7
  assign controlled_buffer_8_out = controlled_buffer_4_out ? in_7 : 1'bz;  // Controlled_Buffer controlled_buffer_8
  and and_1 (and_1_out, in_9, not_1_out);
  assign out_11 = and_1_out ? controlled_buffer_5_out : 1'bz;  // Controlled_Buffer controlled_buffer_9
  assign out_12 = and_1_out ? controlled_buffer_6_out : 1'bz;  // Controlled_Buffer controlled_buffer_10
  assign out_13 = and_1_out ? controlled_buffer_7_out : 1'bz;  // Controlled_Buffer controlled_buffer_11
  assign out_14 = and_1_out ? controlled_buffer_8_out : 1'bz;  // Controlled_Buffer controlled_buffer_12
endmodule

module sub74HC173 (
  input  in_1,
  input  in_2,
  input  in_3,
  input  in_4,
  input  in_5,
  input  in_6,
  input  in_7,
  input  in_8,
  input  in_9,
  input  in_10,
  input  in_11,
  input  in_12,
  output out_13,
  output out_14,
  output out_15,
  output out_16
);

  wire and_1_out, and_2_out, and_3_out, and_4_out, and_5_out, and_6_out, and_7_out, and_8_out, and_9_out,
       and_10_out, and_11_out, controlled_buffer_1_out, controlled_buffer_3_out, controlled_buffer_5_out,
       controlled_buffer_7_out, d_ff_1_q, d_ff_1_qn, d_ff_2_q, d_ff_2_qn, d_ff_3_q, d_ff_3_qn, d_ff_4_q,
       d_ff_4_qn, not_1_out, not_2_out, not_3_out, not_4_out, not_5_out, not_6_out, not_7_out, not_8_out,
       not_9_out, not_10_out, or_1_out, or_2_out, or_3_out, or_4_out;

  not not_1 (not_1_out, in_5);
  and and_1 (and_1_out, not_1_out, not_2_out);
  not not_2 (not_2_out, in_6);
  not not_3 (not_3_out, in_9);
  and and_2 (and_2_out, not_3_out, not_4_out);
  not not_4 (not_4_out, in_10);
  and and_3 (and_3_out, in_11, not_5_out);
  not not_5 (not_5_out, in_12);
  not not_6 (not_6_out, and_1_out);
  assign controlled_buffer_1_out = and_3_out ? in_1 : 1'bz;  // Controlled_Buffer controlled_buffer_1
  and and_4 (and_4_out, and_1_out, controlled_buffer_1_out);
  and and_5 (and_5_out, not_6_out, d_ff_1_q);
  or or_1 (or_1_out, and_4_out, and_5_out);
  D_Flip_Flop d_ff_1 (.D(or_1_out), .clk(in_7), .Q(d_ff_1_q), .Qn(d_ff_1_qn), .reset(in_8));  // open: preset
  not not_7 (not_7_out, d_ff_1_qn);
  assign out_13 = and_2_out ? not_7_out : 1'bz;  // Controlled_Buffer controlled_buffer_2
  assign controlled_buffer_3_out = and_3_out ? in_2 : 1'bz;  // Controlled_Buffer controlled_buffer_3
  and and_6 (and_6_out, and_1_out, controlled_buffer_3_out);
  and and_7 (and_7_out, not_6_out, d_ff_2_q);
  or or_2 (or_2_out, and_6_out, and_7_out);
  D_Flip_Flop d_ff_2 (.D(or_2_out), .clk(in_7), .Q(d_ff_2_q), .Qn(d_ff_2_qn), .reset(in_8));  // open: preset
  not not_8 (not_8_out, d_ff_2_qn);
  assign out_14 = and_2_out ? not_8_out : 1'bz;  // Controlled_Buffer controlled_buffer_4
  assign controlled_buffer_5_out = and_3_out ? in_3 : 1'bz;  // Controlled_Buffer controlled_buffer_5
  and and_8 (and_8_out, and_1_out, controlled_buffer_5_out);
  and and_9 (and_9_out, not_6_out, d_ff_3_q);
  or or_3 (or_3_out, and_8_out, and_9_out);
  D_Flip_Flop d_ff_3 (.D(or_3_out), .clk(in_7), .Q(d_ff_3_q), .Qn(d_ff_3_qn), .reset(in_8));  // open: preset
  not not_9 (not_9_out, d_ff_3_qn);
  assign out_15 = and_2_out ? not_9_out : 1'bz;  // Controlled_Buffer controlled_buffer_6
  assign controlled_buffer_7_out = and_3_out ? in_4 : 1'bz;  // Controlled_Buffer controlled_buffer_7
  and and_10 (and_10_out, and_1_out, controlled_buffer_7_out);
  and and_11 (and_11_out, not_6_out, d_ff_4_q);
  or or_4 (or_4_out, and_10_out, and_11_out);
  D_Flip_Flop d_ff_4 (.D(or_4_out), .clk(in_7), .Q(d_ff_4_q), .Qn(d_ff_4_qn), .reset(in_8));  // open: preset
  not not_10 (not_10_out, d_ff_4_qn);
  assign out_16 = and_2_out ? not_10_out : 1'bz;  // Controlled_Buffer controlled_buffer_8
endmodule

module sub74HC191 (
  input  in_1,
  input  in_2,
  input  in_3,
  input  in_4,
  input  in_5,
  input  in_6,
  input  in_7,
  input  in_8,
  input  in_9,
  input  in_10,
  output out_11,
  output out_12,
  output out_13,
  output out_14,
  output out_15,
  output out_16
);

  wire and_1_out, and_2_out, and_3_out, and_4_out, and_5_out, and_6_out, and_7_out, and_8_out, and_9_out,
       and_10_out, and_11_out, and_12_out, and_13_out, and_14_out, and_15_out, controlled_buffer_1_out,
       controlled_buffer_3_out, controlled_buffer_5_out, controlled_buffer_7_out, j_k_ff_1_q, j_k_ff_1_qn,
       j_k_ff_2_q, j_k_ff_2_qn, j_k_ff_3_q, j_k_ff_3_qn, j_k_ff_4_q, j_k_ff_4_qn, nand_2_out, nand_3_out,
       nand_4_out, nand_5_out, not_1_out, not_2_out, not_3_out, not_4_out, not_5_out, not_6_out, not_7_out,
       not_8_out, not_9_out, not_10_out, not_11_out, not_12_out, not_13_out, not_14_out, or_2_out, or_3_out,
       or_4_out;

  not not_1 (not_1_out, in_5);
  not not_2 (not_2_out, in_6);
  not not_3 (not_3_out, in_10);
  not not_4 (not_4_out, not_8_out);
  not not_5 (not_5_out, in_7);
  not not_6 (not_6_out, in_7);
  not not_7 (not_7_out, not_2_out);
  not not_8 (not_8_out, not_2_out);
  not not_9 (not_9_out, in_7);
  not not_10 (not_10_out, in_8);
  and and_1 (and_1_out, in_9, not_3_out);
  and and_2 (and_2_out, not_4_out, not_5_out);
  and and_3 (and_3_out, not_6_out, not_7_out);
  nand nand_1 (out_15, not_10_out, not_9_out, out_16);
  and and_4 (and_4_out, not_2_out, j_k_ff_1_q, j_k_ff_2_q, j_k_ff_3_q, j_k_ff_4_q);
  or or_1 (out_16, and_4_out, and_5_out);
  and and_5 (and_5_out, not_8_out, j_k_ff_1_qn, j_k_ff_2_qn, j_k_ff_3_qn, j_k_ff_4_qn);
  assign controlled_buffer_1_out = and_1_out ? in_1 : 1'bz;  // Controlled_Buffer controlled_buffer_1
  nand nand_2 (nand_2_out, not_1_out, controlled_buffer_1_out);
  not not_11 (not_11_out, nand_2_out);
  J_K_Flip_Flop #(.trigger("falling")) j_k_ff_1 (
    .J(not_9_out), .K(not_9_out), .clk(not_10_out), .Q(j_k_ff_1_q), .Qn(j_k_ff_1_qn), .preset(not_11_out),
    .reset(and_6_out));
  and and_6 (and_6_out, nand_2_out, not_1_out);
  assign out_11 = and_1_out ? j_k_ff_1_q : 1'bz;  // Controlled_Buffer controlled_buffer_2
  and and_7 (and_7_out, and_3_out, j_k_ff_1_qn);
  or or_2 (or_2_out, and_7_out, and_8_out);
  and and_8 (and_8_out, j_k_ff_1_q, and_2_out);
  assign controlled_buffer_3_out = and_1_out ? in_2 : 1'bz;  // Controlled_Buffer controlled_buffer_3
  nand nand_3 (nand_3_out, not_1_out, controlled_buffer_3_out);
  not not_12 (not_12_out, nand_3_out);
  J_K_Flip_Flop #(.trigger("falling")) j_k_ff_2 (
    .J(or_2_out), .K(or_2_out), .clk(not_10_out), .Q(j_k_ff_2_q), .Qn(j_k_ff_2_qn), .preset(not_12_out),
    .reset(and_9_out));
  and and_9 (and_9_out, nand_3_out, not_1_out);
  assign out_12 = and_1_out ? j_k_ff_2_q : 1'bz;  // Controlled_Buffer controlled_buffer_4
  and and_10 (and_10_out, and_3_out, j_k_ff_1_qn, j_k_ff_2_qn);
  and and_11 (and_11_out, j_k_ff_1_q, j_k_ff_2_q, and_2_out);
  or or_3 (or_3_out, and_10_out, and_11_out);
  assign controlled_buffer_5_out = and_1_out ? in_3 : 1'bz;  // Controlled_Buffer controlled_buffer_5
  nand nand_4 (nand_4_out, not_1_out, controlled_buffer_5_out);
  not not_13 (not_13_out, nand_4_out);
  J_K_Flip_Flop #(.trigger("falling")) j_k_ff_3 (
    .J(or_3_out), .K(or_3_out), .clk(not_10_out), .Q(j_k_ff_3_q), .Qn(j_k_ff_3_qn), .preset(not_13_out),
    .reset(and_12_out));
  and and_12 (and_12_out, nand_4_out, not_1_out);
  assign out_13 = and_1_out ? j_k_ff_3_q : 1'bz;  // Controlled_Buffer controlled_buffer_6
  and and_13 (and_13_out, and_3_out, j_k_ff_1_qn, j_k_ff_2_qn, j_k_ff_3_qn);
  or or_4 (or_4_out, and_13_out, and_14_out);
  and and_14 (and_14_out, j_k_ff_1_q, j_k_ff_2_q, j_k_ff_3_q, and_2_out);
  assign controlled_buffer_7_out = and_1_out ? in_4 : 1'bz;  // Controlled_Buffer controlled_buffer_7
  nand nand_5 (nand_5_out, not_1_out, controlled_buffer_7_out);
  not not_14 (not_14_out, nand_5_out);
  J_K_Flip_Flop #(.trigger("falling")) j_k_ff_4 (
    .J(or_4_out), .K(or_4_out), .clk(not_10_out), .Q(j_k_ff_4_q), .Qn(j_k_ff_4_qn), .preset(not_14_out),
    .reset(and_15_out));
  and and_15 (and_15_out, nand_5_out, not_1_out);
  assign out_14 = and_1_out ? j_k_ff_4_q : 1'bz;  // Controlled_Buffer controlled_buffer_8
endmodule

module sub74HC154 (
  input  in_1,
  input  in_2,
  input  in_3,
  input  in_4,
  input  in_5,
  input  in_6,
  output out_7,
  output out_8,
  output out_9,
  output out_10,
  output out_11,
  output out_12,
  output out_13,
  output out_14,
  output out_15,
  output out_16,
  output out_17,
  output out_18,
  output out_19,
  output out_20,
  output out_21,
  output out_22
);

  wire and_1_out, decoder_1_out0, decoder_1_out1, decoder_1_out2, decoder_1_out3, decoder_1_out4,
       decoder_1_out5, decoder_1_out6, decoder_1_out7, decoder_1_out8, decoder_1_out9, decoder_1_out10,
       decoder_1_out11, decoder_1_out12, decoder_1_out13, decoder_1_out14, decoder_1_out15, not_1_out,
       not_2_out;

  not not_1 (not_1_out, in_1);
  and and_1 (and_1_out, not_1_out, not_2_out);
  not not_2 (not_2_out, in_2);
  Decoder #(.select(4)) decoder_1 (
    .out0(decoder_1_out0), .out1(decoder_1_out1), .out2(decoder_1_out2), .out3(decoder_1_out3),
    .out4(decoder_1_out4), .out5(decoder_1_out5), .out6(decoder_1_out6), .out7(decoder_1_out7),
    .out8(decoder_1_out8), .out9(decoder_1_out9), .out10(decoder_1_out10), .out11(decoder_1_out11),
    .out12(decoder_1_out12), .out13(decoder_1_out13), .out14(decoder_1_out14), .out15(decoder_1_out15),
    .sel({in_6, in_5, in_4, in_3}), .en(and_1_out));
  not not_3 (out_7, decoder_1_out0);
  not not_4 (out_17, decoder_1_out10);
  not not_5 (out_8, decoder_1_out1);
  not not_6 (out_9, decoder_1_out2);
  not not_7 (out_15, decoder_1_out8);
  not not_8 (out_16, decoder_1_out9);
  not not_9 (out_18, decoder_1_out11);
  not not_10 (out_19, decoder_1_out12);
  not not_11 (out_10, decoder_1_out3);
  not not_12 (out_11, decoder_1_out4);
  not not_13 (out_13, decoder_1_out6);
  not not_14 (out_14, decoder_1_out7);
  not not_15 (out_20, decoder_1_out13);
  not not_16 (out_21, decoder_1_out14);
  not not_17 (out_12, decoder_1_out5);
  not not_18 (out_22, decoder_1_out15);
endmodule
