// Logisim project ALU.circ as structural Verilog: 1 circuit, main circuit main
module main (
);

  wire and_1_out, and_2_out, and_3_out, and_4_out, and_5_out, and_6_out, and_7_out, and_8_out, and_9_out,
       and_10_out, and_11_out, and_12_out, and_13_out, and_14_out, and_15_out, and_16_out, and_17_out,
       and_18_out, and_19_out, and_20_out, and_21_out, and_22_out, and_23_out, and_24_out, clock_1_out,
       controlled_buffer_1_out, controlled_buffer_2_out, controlled_buffer_3_out, controlled_buffer_4_out,
       controlled_buffer_5_out, controlled_buffer_6_out, controlled_buffer_8_out, controlled_buffer_10_out,
       controlled_buffer_12_out, controlled_buffer_14_out, controlled_buffer_20_out,
       controlled_buffer_21_out, controlled_buffer_22_out, controlled_buffer_23_out,
       controlled_buffer_24_out, controlled_buffer_25_out, controlled_buffer_26_out,
       controlled_buffer_27_out, controlled_buffer_28_out, controlled_buffer_29_out,
       controlled_buffer_30_out, controlled_buffer_31_out, controlled_buffer_32_out,
       controlled_buffer_34_out, controlled_buffer_48_out, controlled_buffer_50_out,
       controlled_buffer_54_out, controlled_buffer_55_out, controlled_buffer_56_out,
       controlled_buffer_57_out, controlled_buffer_67_out, controlled_buffer_68_out,
       controlled_buffer_71_out, controlled_buffer_78_out, controlled_buffer_80_out,
       controlled_buffer_82_out, controlled_buffer_86_out, controlled_buffer_89_out,
       controlled_buffer_93_out, controlled_buffer_95_out, controlled_buffer_97_out,
       controlled_buffer_103_out, controlled_buffer_105_out, controlled_buffer_107_out, d_ff_1_q, d_ff_1_qn,
       d_ff_2_qn, d_ff_3_qn, d_ff_4_q, d_ff_5_q, d_ff_6_q, d_ff_6_qn, d_ff_7_q, d_ff_8_q, d_ff_9_q,
       d_ff_9_qn, d_ff_10_q, d_ff_11_q, d_ff_12_q, d_ff_12_qn, d_ff_13_q, d_ff_14_q, d_ff_14_qn,
       decoder_1_out3, decoder_1_out4, decoder_1_out5, decoder_1_out6, decoder_1_out7, decoder_1_out8,
       decoder_1_out9, decoder_1_out10, decoder_2_out0, decoder_2_out2, decoder_2_out3, dipswitch_2_sw1,
       dipswitch_2_sw2, dipswitch_2_sw3, dipswitch_2_sw4, dipswitch_3_sw1, dipswitch_3_sw2, dipswitch_3_sw3,
       dipswitch_3_sw4, not_1_out, not_2_out, not_3_out, not_4_out, not_5_out, not_6_out, not_7_out,
       not_8_out, not_9_out, not_10_out, not_11_out, not_12_out, not_13_out, not_14_out, not_15_out,
       not_16_out, not_17_out, not_18_out, not_19_out, or_1_out, or_2_out, or_3_out, or_4_out, or_5_out,
       or_6_out, or_7_out, or_8_out, or_9_out, or_10_out, pull_resistor_1_node, pull_resistor_6_node,
       pull_resistor_15_node, pull_resistor_17_node, pull_resistor_19_node, pull_resistor_21_node,
       pull_resistor_23_node, pull_resistor_25_node, pull_resistor_27_node, pull_resistor_29_node,
       pull_resistor_31_node, pull_resistor_33_node, pull_resistor_35_node, pull_resistor_37_node,
       pull_resistor_39_node, pull_resistor_40_node, xor_1_out, xor_2_out, xor_3_out, xor_4_out, xor_5_out,
       xor_6_out, xor_7_out, xor_8_out, xor_9_out, xor_10_out, xor_11_out, xor_12_out;
  wire [1:0] d_ff_2_q;
  wire [3:0] dipswitch_1_sw4;

  DipSwitch #(.number(4)) dipswitch_1 (
    .sw1(dipswitch_1_sw4[3]), .sw2(dipswitch_1_sw4[2]), .sw3(dipswitch_1_sw4[1]), .sw4(dipswitch_1_sw4[0]));
  Decoder #(.select(4)) decoder_1 (
    .out3(decoder_1_out3), .out4(decoder_1_out4), .out5(decoder_1_out5), .out6(decoder_1_out6),
    .out7(decoder_1_out7), .out8(decoder_1_out8), .out9(decoder_1_out9), .out10(decoder_1_out10),
    .sel(dipswitch_1_sw4));  // open: out0, out1, out2, out11, out12, out13, out14, out15, en
  DipSwitch #(.number(4)) dipswitch_2 (
    .sw1(dipswitch_2_sw1), .sw2(dipswitch_2_sw2), .sw3(dipswitch_2_sw3), .sw4(dipswitch_2_sw4));
  DipSwitch #(.number(4)) dipswitch_3 (
    .sw1(dipswitch_3_sw1), .sw2(dipswitch_3_sw2), .sw3(dipswitch_3_sw3), .sw4(dipswitch_3_sw4));
  Pull_Resistor pull_resistor_1 (.node(pull_resistor_1_node));
  // Switch switch_1: pin names not known; wires that end beside it: 1'b1, pull_resistor_1_node
  Clock clock_1 (.out(clock_1_out));
  D_Flip_Flop #(.trigger("falling")) d_ff_1 (
    .D(d_ff_1_qn), .clk(clock_1_out), .Q(d_ff_1_q), .Qn(d_ff_1_qn));  // open: preset, reset
  D_Flip_Flop #(.trigger("falling")) d_ff_2 (
    .D(d_ff_2_qn), .clk(d_ff_1_q), .Q(d_ff_2_q[0]), .Qn(d_ff_2_qn));  // open: preset, reset
  D_Flip_Flop #(.trigger("falling")) d_ff_3 (
    .D(d_ff_3_qn), .clk(d_ff_2_q[0]), .Q(d_ff_2_q[1]), .Qn(d_ff_3_qn));  // open: preset, reset
  or or_1 (or_1_out, decoder_1_out3, decoder_1_out4, decoder_1_out5);
  Decoder #(.select(2)) decoder_2 (
    .out0(decoder_2_out0), .out2(decoder_2_out2), .out3(decoder_2_out3), .sel(d_ff_2_q));  // open: out1, en
  or or_2 (or_2_out, decoder_1_out3, decoder_1_out4);
  not not_1 (not_1_out, clock_1_out);
  and and_1 (and_1_out, not_1_out, decoder_2_out2);
  assign controlled_buffer_1_out = decoder_1_out5 ? dipswitch_2_sw4 : 1'bz;  // Controlled_Buffer controlled_buffer_1
  assign controlled_buffer_2_out = decoder_1_out5 ? dipswitch_2_sw3 : 1'bz;  // Controlled_Buffer controlled_buffer_2
  assign controlled_buffer_3_out = decoder_1_out5 ? dipswitch_2_sw2 : 1'bz;  // Controlled_Buffer controlled_buffer_3
  assign controlled_buffer_4_out = decoder_1_out5 ? dipswitch_2_sw1 : 1'bz;  // Controlled_Buffer controlled_buffer_4
  D_Flip_Flop #(.trigger("falling")) d_ff_4 (
    .D(decoder_1_out9), .clk(and_1_out), .Q(d_ff_4_q), .reset(and_2_out));  // open: Qn, preset
  assign controlled_buffer_5_out = decoder_1_out9 ? pull_resistor_1_node : 1'bz;  // Controlled_Buffer controlled_buffer_5
  assign controlled_buffer_6_out = decoder_1_out9 ? decoder_2_out2 : 1'bz;  // Controlled_Buffer controlled_buffer_6
  not not_2 (not_2_out, clock_1_out);
  not not_3 (not_3_out, clock_1_out);
  not not_4 (not_4_out, clock_1_out);
  assign controlled_buffer_1_out = or_2_out ? dipswitch_2_sw4 : 1'bz;  // Controlled_Buffer controlled_buffer_7
  assign controlled_buffer_8_out = or_2_out ? dipswitch_3_sw4 : 1'bz;  // Controlled_Buffer controlled_buffer_8
  not not_5 (not_5_out, dipswitch_3_sw4);
  assign controlled_buffer_2_out = or_2_out ? dipswitch_2_sw3 : 1'bz;  // Controlled_Buffer controlled_buffer_9
  assign controlled_buffer_10_out = or_2_out ? dipswitch_3_sw3 : 1'bz;  // Controlled_Buffer controlled_buffer_10
  not not_6 (not_6_out, dipswitch_3_sw3);
  assign controlled_buffer_3_out = or_2_out ? dipswitch_2_sw2 : 1'bz;  // Controlled_Buffer controlled_buffer_11
  assign controlled_buffer_12_out = or_2_out ? dipswitch_3_sw2 : 1'bz;  // Controlled_Buffer controlled_buffer_12
  not not_7 (not_7_out, dipswitch_3_sw2);
  assign controlled_buffer_4_out = or_2_out ? dipswitch_2_sw1 : 1'bz;  // Controlled_Buffer controlled_buffer_13
  assign controlled_buffer_14_out = or_2_out ? dipswitch_3_sw1 : 1'bz;  // Controlled_Buffer controlled_buffer_14
  not not_8 (not_8_out, dipswitch_3_sw1);
  not not_9 (not_9_out, d_ff_4_q);
  Pull_Resistor pull_resistor_2 (.node(controlled_buffer_5_out));
  and and_2 (and_2_out, decoder_2_out0, d_ff_1_q);
  Pull_Resistor pull_resistor_3 (.node(controlled_buffer_6_out));
  and and_3 (and_3_out, not_2_out, decoder_1_out9, decoder_2_out2);
  D_Flip_Flop #(.trigger("falling")) d_ff_5 (
    .D(decoder_1_out10), .clk(and_4_out), .Q(d_ff_5_q), .reset(and_5_out));  // open: Qn, preset
  and and_4 (and_4_out, not_3_out, decoder_2_out2);
  and and_5 (and_5_out, decoder_2_out0, d_ff_1_q);
  and and_6 (and_6_out, not_4_out, decoder_1_out10, decoder_2_out2);
  Pull_Resistor pull_resistor_4 (.node(controlled_buffer_1_out));
  Pull_Resistor pull_resistor_5 (.node(controlled_buffer_8_out));
  assign controlled_buffer_8_out = decoder_1_out5 ? not_5_out : 1'bz;  // Controlled_Buffer controlled_buffer_15
  Pull_Resistor pull_resistor_6 (.node(pull_resistor_6_node));
  assign pull_resistor_6_node = decoder_1_out5 ? 1'b1 : 1'bz;  // Controlled_Buffer controlled_buffer_16
  Pull_Resistor pull_resistor_7 (.node(controlled_buffer_2_out));
  Pull_Resistor pull_resistor_8 (.node(controlled_buffer_10_out));
  assign controlled_buffer_10_out = decoder_1_out5 ? not_6_out : 1'bz;  // Controlled_Buffer controlled_buffer_17
  Pull_Resistor pull_resistor_9 (.node(controlled_buffer_3_out));
  Pull_Resistor pull_resistor_10 (.node(controlled_buffer_12_out));
  assign controlled_buffer_12_out = decoder_1_out5 ? not_7_out : 1'bz;  // Controlled_Buffer controlled_buffer_18
  Pull_Resistor pull_resistor_11 (.node(controlled_buffer_4_out));
  Pull_Resistor pull_resistor_12 (.node(controlled_buffer_14_out));
  assign controlled_buffer_14_out = decoder_1_out5 ? not_8_out : 1'bz;  // Controlled_Buffer controlled_buffer_19
  and and_7 (and_7_out, decoder_1_out9, not_9_out);
  not not_10 (not_10_out, controlled_buffer_5_out);
  and and_8 (and_8_out, d_ff_1_q, controlled_buffer_6_out);
  and and_9 (and_9_out, decoder_1_out9, decoder_2_out3);
  and and_10 (and_10_out, decoder_1_out10, not_11_out);
  not not_11 (not_11_out, d_ff_5_q);
  and and_11 (and_11_out, d_ff_1_q, decoder_2_out2);
  xor xor_1 (xor_1_out, controlled_buffer_1_out, controlled_buffer_8_out);
  xor xor_2 (xor_2_out, controlled_buffer_2_out, controlled_buffer_10_out);
  xor xor_3 (xor_3_out, controlled_buffer_3_out, controlled_buffer_12_out);
  xor xor_4 (xor_4_out, controlled_buffer_4_out, controlled_buffer_14_out);
  assign controlled_buffer_20_out = decoder_1_out6 ? dipswitch_2_sw1 : 1'bz;  // Controlled_Buffer controlled_buffer_20
  assign controlled_buffer_21_out = decoder_1_out6 ? dipswitch_2_sw2 : 1'bz;  // Controlled_Buffer controlled_buffer_21
  assign controlled_buffer_22_out = decoder_1_out6 ? dipswitch_2_sw3 : 1'bz;  // Controlled_Buffer controlled_buffer_22
  assign controlled_buffer_23_out = decoder_1_out6 ? dipswitch_2_sw4 : 1'bz;  // Controlled_Buffer controlled_buffer_23
  assign controlled_buffer_24_out = decoder_1_out7 ? dipswitch_2_sw1 : 1'bz;  // Controlled_Buffer controlled_buffer_24
  assign controlled_buffer_25_out = decoder_1_out7 ? dipswitch_2_sw2 : 1'bz;  // Controlled_Buffer controlled_buffer_25
  assign controlled_buffer_26_out = decoder_1_out7 ? dipswitch_2_sw3 : 1'bz;  // Controlled_Buffer controlled_buffer_26
  assign controlled_buffer_27_out = decoder_1_out7 ? dipswitch_2_sw4 : 1'bz;  // Controlled_Buffer controlled_buffer_27
  assign controlled_buffer_28_out = decoder_1_out8 ? dipswitch_2_sw1 : 1'bz;  // Controlled_Buffer controlled_buffer_28
  assign controlled_buffer_29_out = decoder_1_out8 ? dipswitch_2_sw2 : 1'bz;  // Controlled_Buffer controlled_buffer_29
  assign controlled_buffer_30_out = decoder_1_out8 ? dipswitch_2_sw3 : 1'bz;  // Controlled_Buffer controlled_buffer_30
  assign controlled_buffer_31_out = decoder_1_out8 ? dipswitch_2_sw4 : 1'bz;  // Controlled_Buffer controlled_buffer_31
  assign controlled_buffer_32_out = not_10_out ? and_8_out : 1'bz;  // Controlled_Buffer controlled_buffer_32
  Pull_Resistor pull_resistor_13 (.node(controlled_buffer_32_out));
  not not_12 (not_12_out, and_8_out);
  assign controlled_buffer_32_out = controlled_buffer_5_out ? not_12_out : 1'bz;  // Controlled_Buffer controlled_buffer_33
  not not_13 (not_13_out, and_10_out);
  assign controlled_buffer_34_out = not_13_out ? and_11_out : 1'bz;  // Controlled_Buffer controlled_buffer_34
  assign controlled_buffer_34_out = and_10_out ? and_6_out : 1'bz;  // Controlled_Buffer controlled_buffer_35
  and and_12 (and_12_out, decoder_1_out10, decoder_2_out3);
  xor xor_5 (xor_5_out, xor_1_out, pull_resistor_6_node);
  and and_13 (and_13_out, pull_resistor_6_node, xor_1_out);
  or or_3 (or_3_out, and_13_out, and_14_out);
  and and_14 (and_14_out, controlled_buffer_8_out, controlled_buffer_1_out);
  xor xor_6 (xor_6_out, xor_2_out, or_3_out);
  and and_15 (and_15_out, or_3_out, xor_2_out);
  or or_4 (or_4_out, and_15_out, and_16_out);
  and and_16 (and_16_out, controlled_buffer_10_out, controlled_buffer_2_out);
  xor xor_7 (xor_7_out, xor_3_out, or_4_out);
  and and_17 (and_17_out, or_4_out, xor_3_out);
  or or_5 (or_5_out, and_17_out, and_18_out);
  and and_18 (and_18_out, controlled_buffer_12_out, controlled_buffer_3_out);
  xor xor_8 (xor_8_out, xor_4_out, or_5_out);
  and and_19 (and_19_out, or_5_out, xor_4_out);
  or or_6 (or_6_out, and_19_out, and_20_out);
  and and_20 (and_20_out, controlled_buffer_14_out, controlled_buffer_4_out);
  Pull_Resistor pull_resistor_14 (.node(controlled_buffer_20_out));
  Pull_Resistor pull_resistor_15 (.node(pull_resistor_15_node));
  assign pull_resistor_15_node = decoder_1_out6 ? dipswitch_3_sw1 : 1'bz;  // Controlled_Buffer controlled_buffer_36
  Pull_Resistor pull_resistor_16 (.node(controlled_buffer_21_out));
  Pull_Resistor pull_resistor_17 (.node(pull_resistor_17_node));
  assign pull_resistor_17_node = decoder_1_out6 ? dipswitch_3_sw2 : 1'bz;  // Controlled_Buffer controlled_buffer_37
  Pull_Resistor pull_resistor_18 (.node(controlled_buffer_22_out));
  Pull_Resistor pull_resistor_19 (.node(pull_resistor_19_node));
  assign pull_resistor_19_node = decoder_1_out6 ? dipswitch_3_sw3 : 1'bz;  // Controlled_Buffer controlled_buffer_38
  Pull_Resistor pull_resistor_20 (.node(controlled_buffer_23_out));
  Pull_Resistor pull_resistor_21 (.node(pull_resistor_21_node));
  assign pull_resistor_21_node = decoder_1_out6 ? dipswitch_3_sw4 : 1'bz;  // Controlled_Buffer controlled_buffer_39
  Pull_Resistor pull_resistor_22 (.node(controlled_buffer_24_out));
  Pull_Resistor pull_resistor_23 (.node(pull_resistor_23_node));
  assign pull_resistor_23_node = decoder_1_out7 ? dipswitch_3_sw1 : 1'bz;  // Controlled_Buffer controlled_buffer_40
  Pull_Resistor pull_resistor_24 (.node(controlled_buffer_25_out));
  Pull_Resistor pull_resistor_25 (.node(pull_resistor_25_node));
  assign pull_resistor_25_node = decoder_1_out7 ? dipswitch_3_sw2 : 1'bz;  // Controlled_Buffer controlled_buffer_41
  Pull_Resistor pull_resistor_26 (.node(controlled_buffer_26_out));
  Pull_Resistor pull_resistor_27 (.node(pull_resistor_27_node));
  assign pull_resistor_27_node = decoder_1_out7 ? dipswitch_3_sw3 : 1'bz;  // Controlled_Buffer controlled_buffer_42
  Pull_Resistor pull_resistor_28 (.node(controlled_buffer_27_out));
  Pull_Resistor pull_resistor_29 (.node(pull_resistor_29_node));
  assign pull_resistor_29_node = decoder_1_out7 ? dipswitch_3_sw4 : 1'bz;  // Controlled_Buffer controlled_buffer_43
  Pull_Resistor pull_resistor_30 (.node(controlled_buffer_28_out));
  Pull_Resistor pull_resistor_31 (.node(pull_resistor_31_node));
  assign pull_resistor_31_node = decoder_1_out8 ? dipswitch_3_sw1 : 1'bz;  // Controlled_Buffer controlled_buffer_44
  Pull_Resistor pull_resistor_32 (.node(controlled_buffer_29_out));
  Pull_Resistor pull_resistor_33 (.node(pull_resistor_33_node));
  assign pull_resistor_33_node = decoder_1_out8 ? dipswitch_3_sw2 : 1'bz;  // Controlled_Buffer controlled_buffer_45
  Pull_Resistor pull_resistor_34 (.node(controlled_buffer_30_out));
  Pull_Resistor pull_resistor_35 (.node(pull_resistor_35_node));
  assign pull_resistor_35_node = decoder_1_out8 ? dipswitch_3_sw3 : 1'bz;  // Controlled_Buffer controlled_buffer_46
  Pull_Resistor pull_resistor_36 (.node(controlled_buffer_31_out));
  Pull_Resistor pull_resistor_37 (.node(pull_resistor_37_node));
  assign pull_resistor_37_node = decoder_1_out8 ? dipswitch_3_sw4 : 1'bz;  // Controlled_Buffer controlled_buffer_47
  not not_14 (not_14_out, and_7_out);
  assign controlled_buffer_48_out = and_7_out ? dipswitch_2_sw4 : 1'bz;  // Controlled_Buffer controlled_buffer_48
  D_Flip_Flop d_ff_6 (
    .D(controlled_buffer_48_out), .clk(controlled_buffer_50_out), .Q(d_ff_6_q), .Qn(d_ff_6_qn));  // open: preset, reset
  Pull_Resistor pull_resistor_38 (.node(controlled_buffer_48_out));
  assign controlled_buffer_48_out = not_14_out ? d_ff_6_qn : 1'bz;  // Controlled_Buffer controlled_buffer_49
  assign controlled_buffer_50_out = not_15_out ? controlled_buffer_32_out : 1'bz;  // Controlled_Buffer controlled_buffer_50
  assign controlled_buffer_50_out = and_7_out ? and_3_out : 1'bz;  // Controlled_Buffer controlled_buffer_51
  not not_15 (not_15_out, and_7_out);
  Pull_Resistor pull_resistor_39 (.node(pull_resistor_39_node));
  assign pull_resistor_39_node = not_13_out ? pull_resistor_1_node : 1'bz;  // Controlled_Buffer controlled_buffer_52
  D_Flip_Flop d_ff_7 (.D(or_6_out), .clk(pull_resistor_40_node), .Q(d_ff_7_q));  // open: Qn, preset, reset
  Pull_Resistor pull_resistor_40 (.node(pull_resistor_40_node));
  assign pull_resistor_40_node = or_2_out ? decoder_2_out2 : 1'bz;  // Controlled_Buffer controlled_buffer_53
  and and_21 (and_21_out, controlled_buffer_20_out, pull_resistor_15_node);
  assign controlled_buffer_54_out = decoder_1_out6 ? and_21_out : 1'bz;  // Controlled_Buffer controlled_buffer_54
  and and_22 (and_22_out, controlled_buffer_21_out, pull_resistor_17_node);
  assign controlled_buffer_55_out = decoder_1_out6 ? and_22_out : 1'bz;  // Controlled_Buffer controlled_buffer_55
  and and_23 (and_23_out, controlled_buffer_22_out, pull_resistor_19_node);
  assign controlled_buffer_56_out = decoder_1_out6 ? and_23_out : 1'bz;  // Controlled_Buffer controlled_buffer_56
  and and_24 (and_24_out, controlled_buffer_23_out, pull_resistor_21_node);
  assign controlled_buffer_57_out = decoder_1_out6 ? and_24_out : 1'bz;  // Controlled_Buffer controlled_buffer_57
  or or_7 (or_7_out, controlled_buffer_24_out, pull_resistor_23_node);
  assign controlled_buffer_54_out = decoder_1_out7 ? or_7_out : 1'bz;  // Controlled_Buffer controlled_buffer_58
  or or_8 (or_8_out, controlled_buffer_25_out, pull_resistor_25_node);
  assign controlled_buffer_55_out = decoder_1_out7 ? or_8_out : 1'bz;  // Controlled_Buffer controlled_buffer_59
  or or_9 (or_9_out, controlled_buffer_26_out, pull_resistor_27_node);
  assign controlled_buffer_56_out = decoder_1_out7 ? or_9_out : 1'bz;  // Controlled_Buffer controlled_buffer_60
  or or_10 (or_10_out, controlled_buffer_27_out, pull_resistor_29_node);
  assign controlled_buffer_57_out = decoder_1_out7 ? or_10_out : 1'bz;  // Controlled_Buffer controlled_buffer_61
  xor xor_9 (xor_9_out, controlled_buffer_28_out, pull_resistor_31_node);
  assign controlled_buffer_54_out = decoder_1_out8 ? xor_9_out : 1'bz;  // Controlled_Buffer controlled_buffer_62
  xor xor_10 (xor_10_out, controlled_buffer_29_out, pull_resistor_33_node);
  assign controlled_buffer_55_out = decoder_1_out8 ? xor_10_out : 1'bz;  // Controlled_Buffer controlled_buffer_63
  xor xor_11 (xor_11_out, controlled_buffer_30_out, pull_resistor_35_node);
  assign controlled_buffer_56_out = decoder_1_out8 ? xor_11_out : 1'bz;  // Controlled_Buffer controlled_buffer_64
  xor xor_12 (xor_12_out, controlled_buffer_31_out, pull_resistor_37_node);
  assign controlled_buffer_57_out = decoder_1_out8 ? xor_12_out : 1'bz;  // Controlled_Buffer controlled_buffer_65
  assign controlled_buffer_57_out = and_9_out ? d_ff_6_q : 1'bz;  // Controlled_Buffer controlled_buffer_66
  assign controlled_buffer_67_out = and_10_out ? dipswitch_2_sw4 : 1'bz;  // Controlled_Buffer controlled_buffer_67
  not not_16 (not_16_out, pull_resistor_39_node);
  assign controlled_buffer_68_out = not_13_out ? not_16_out : 1'bz;  // Controlled_Buffer controlled_buffer_68
  Pull_Resistor pull_resistor_41 (.node(controlled_buffer_67_out));
  assign controlled_buffer_67_out = pull_resistor_39_node ? 1'b0 : 1'bz;  // Controlled_Buffer controlled_buffer_69
  assign pull_resistor_6_node = decoder_1_out4 ? d_ff_7_q : 1'bz;  // Controlled_Buffer controlled_buffer_70
  assign controlled_buffer_71_out = not_10_out ? d_ff_6_q : 1'bz;  // Controlled_Buffer controlled_buffer_71
  Pull_Resistor pull_resistor_42 (.node(controlled_buffer_71_out));
  not not_17 (not_17_out, d_ff_6_q);
  assign controlled_buffer_71_out = controlled_buffer_5_out ? not_17_out : 1'bz;  // Controlled_Buffer controlled_buffer_72
  D_Flip_Flop d_ff_8 (
    .D(controlled_buffer_67_out), .clk(controlled_buffer_34_out), .Q(d_ff_8_q));  // open: Qn, preset, reset
  assign controlled_buffer_57_out = and_12_out ? d_ff_8_q : 1'bz;  // Controlled_Buffer controlled_buffer_73
  assign controlled_buffer_57_out = or_1_out ? xor_5_out : 1'bz;  // Controlled_Buffer controlled_buffer_74
  assign controlled_buffer_56_out = or_1_out ? xor_6_out : 1'bz;  // Controlled_Buffer controlled_buffer_75
  assign controlled_buffer_55_out = or_1_out ? xor_7_out : 1'bz;  // Controlled_Buffer controlled_buffer_76
  assign controlled_buffer_54_out = or_1_out ? xor_8_out : 1'bz;  // Controlled_Buffer controlled_buffer_77
  Pull_Resistor pull_resistor_43 (.node(or_1_out));
  assign controlled_buffer_78_out = and_7_out ? dipswitch_2_sw3 : 1'bz;  // Controlled_Buffer controlled_buffer_78
  D_Flip_Flop d_ff_9 (
    .D(controlled_buffer_78_out), .clk(controlled_buffer_80_out), .Q(d_ff_9_q), .Qn(d_ff_9_qn));  // open: preset, reset
  assign controlled_buffer_78_out = not_14_out ? d_ff_9_qn : 1'bz;  // Controlled_Buffer controlled_buffer_79
  assign controlled_buffer_80_out = not_15_out ? controlled_buffer_71_out : 1'bz;  // Controlled_Buffer controlled_buffer_80
  assign controlled_buffer_80_out = and_7_out ? and_3_out : 1'bz;  // Controlled_Buffer controlled_buffer_81
  assign controlled_buffer_82_out = and_10_out ? dipswitch_2_sw3 : 1'bz;  // Controlled_Buffer controlled_buffer_82
  assign controlled_buffer_67_out = controlled_buffer_68_out ? d_ff_10_q : 1'bz;  // Controlled_Buffer controlled_buffer_83
  D_Flip_Flop d_ff_10 (
    .D(controlled_buffer_82_out), .clk(controlled_buffer_34_out), .Q(d_ff_10_q));  // open: Qn, preset, reset
  Pull_Resistor pull_resistor_44 (.node(controlled_buffer_82_out));
  assign controlled_buffer_82_out = pull_resistor_39_node ? d_ff_8_q : 1'bz;  // Controlled_Buffer controlled_buffer_84
  assign controlled_buffer_56_out = and_9_out ? d_ff_9_q : 1'bz;  // Controlled_Buffer controlled_buffer_85
  assign controlled_buffer_86_out = and_10_out ? dipswitch_2_sw2 : 1'bz;  // Controlled_Buffer controlled_buffer_86
  Pull_Resistor pull_resistor_45 (.node(controlled_buffer_86_out));
  assign controlled_buffer_86_out = pull_resistor_39_node ? d_ff_10_q : 1'bz;  // Controlled_Buffer controlled_buffer_87
  assign controlled_buffer_56_out = and_12_out ? d_ff_10_q : 1'bz;  // Controlled_Buffer controlled_buffer_88
  assign controlled_buffer_89_out = not_10_out ? d_ff_9_q : 1'bz;  // Controlled_Buffer controlled_buffer_89
  Pull_Resistor pull_resistor_46 (.node(controlled_buffer_89_out));
  not not_18 (not_18_out, d_ff_9_q);
  assign controlled_buffer_89_out = controlled_buffer_5_out ? not_18_out : 1'bz;  // Controlled_Buffer controlled_buffer_90
  assign controlled_buffer_82_out = controlled_buffer_68_out ? d_ff_11_q : 1'bz;  // Controlled_Buffer controlled_buffer_91
  D_Flip_Flop d_ff_11 (
    .D(controlled_buffer_86_out), .clk(controlled_buffer_34_out), .Q(d_ff_11_q));  // open: Qn, preset, reset
  assign controlled_buffer_55_out = and_12_out ? d_ff_11_q : 1'bz;  // Controlled_Buffer controlled_buffer_92
  assign controlled_buffer_93_out = and_7_out ? dipswitch_2_sw2 : 1'bz;  // Controlled_Buffer controlled_buffer_93
  D_Flip_Flop d_ff_12 (
    .D(controlled_buffer_93_out), .clk(controlled_buffer_95_out), .Q(d_ff_12_q), .Qn(d_ff_12_qn));  // open: preset, reset
  assign controlled_buffer_93_out = not_14_out ? d_ff_12_qn : 1'bz;  // Controlled_Buffer controlled_buffer_94
  assign controlled_buffer_95_out = not_15_out ? controlled_buffer_89_out : 1'bz;  // Controlled_Buffer controlled_buffer_95
  assign controlled_buffer_95_out = and_7_out ? and_3_out : 1'bz;  // Controlled_Buffer controlled_buffer_96
  assign controlled_buffer_97_out = and_10_out ? dipswitch_2_sw1 : 1'bz;  // Controlled_Buffer controlled_buffer_97
  assign controlled_buffer_86_out = controlled_buffer_68_out ? d_ff_13_q : 1'bz;  // Controlled_Buffer controlled_buffer_98
  D_Flip_Flop d_ff_13 (
    .D(controlled_buffer_97_out), .clk(controlled_buffer_34_out), .Q(d_ff_13_q));  // open: Qn, preset, reset
  Pull_Resistor pull_resistor_47 (.node(controlled_buffer_97_out));
  assign controlled_buffer_97_out = pull_resistor_39_node ? d_ff_11_q : 1'bz;  // Controlled_Buffer controlled_buffer_99
  Pull_Resistor pull_resistor_48 (.node(controlled_buffer_34_out));
  assign controlled_buffer_55_out = and_9_out ? d_ff_12_q : 1'bz;  // Controlled_Buffer controlled_buffer_100
  Pull_Resistor pull_resistor_49 (.node(controlled_buffer_68_out));
  assign controlled_buffer_97_out = controlled_buffer_68_out ? 1'b0 : 1'bz;  // Controlled_Buffer controlled_buffer_101
  assign controlled_buffer_54_out = and_12_out ? d_ff_13_q : 1'bz;  // Controlled_Buffer controlled_buffer_102
  assign controlled_buffer_103_out = not_10_out ? d_ff_12_q : 1'bz;  // Controlled_Buffer controlled_buffer_103
  Pull_Resistor pull_resistor_50 (.node(controlled_buffer_103_out));
  not not_19 (not_19_out, d_ff_12_q);
  assign controlled_buffer_103_out = controlled_buffer_5_out ? not_19_out : 1'bz;  // Controlled_Buffer controlled_buffer_104
  assign controlled_buffer_105_out = and_7_out ? dipswitch_2_sw1 : 1'bz;  // Controlled_Buffer controlled_buffer_105
  D_Flip_Flop d_ff_14 (
    .D(controlled_buffer_105_out), .clk(controlled_buffer_107_out), .Q(d_ff_14_q), .Qn(d_ff_14_qn));  // open: preset, reset
  assign controlled_buffer_105_out = not_14_out ? d_ff_14_qn : 1'bz;  // Controlled_Buffer controlled_buffer_106
  assign controlled_buffer_107_out = not_15_out ? controlled_buffer_103_out : 1'bz;  // Controlled_Buffer controlled_buffer_107
  assign controlled_buffer_107_out = and_7_out ? and_3_out : 1'bz;  // Controlled_Buffer controlled_buffer_108
  assign controlled_buffer_54_out = and_9_out ? d_ff_14_q : 1'bz;  // Controlled_Buffer controlled_buffer_109
  LED led_1 (.in(controlled_buffer_54_out));
  Pull_Resistor pull_resistor_51 (.node(controlled_buffer_54_out));
  LED led_2 (.in(controlled_buffer_55_out));
  LED led_3 (.in(controlled_buffer_56_out));
  LED led_4 (.in(controlled_buffer_57_out));
  Pull_Resistor pull_resistor_52 (.node(controlled_buffer_55_out));
  Pull_Resistor pull_resistor_53 (.node(controlled_buffer_56_out));
  Pull_Resistor pull_resistor_54 (.node(controlled_buffer_57_out));
endmodule
