// Logisim project CPU.circ as structural Verilog: 1 circuit, main circuit main
module main (
);

  wire and_1_out, and_2_out, and_3_out, and_4_out, and_5_out, and_6_out, and_7_out, and_8_out, and_9_out,
       and_10_out, and_11_out, and_12_out, and_13_out, and_14_out, and_15_out, and_16_out, and_17_out,
       and_18_out, and_19_out, and_20_out, and_21_out, and_22_out, and_23_out, and_24_out, and_25_out,
       and_26_out, and_27_out, and_28_out, and_29_out, and_30_out, and_31_out, and_32_out, and_33_out,
       and_34_out, and_35_out, and_36_out, and_37_out, and_38_out, and_39_out, and_40_out, and_41_out,
       clock_1_out, controlled_buffer_22_out, controlled_buffer_23_out, controlled_buffer_24_out,
       controlled_buffer_25_out, controlled_buffer_26_out, controlled_buffer_27_out,
       controlled_buffer_28_out, controlled_buffer_29_out, controlled_buffer_30_out,
       controlled_buffer_31_out, controlled_buffer_32_out, controlled_buffer_33_out,
       controlled_buffer_66_out, controlled_buffer_87_out, controlled_buffer_88_out,
       controlled_buffer_89_out, controlled_buffer_90_out, controlled_buffer_93_out,
       controlled_buffer_94_out, controlled_buffer_95_out, controlled_buffer_103_out,
       controlled_buffer_115_out, controlled_buffer_118_out, controlled_buffer_122_out,
       controlled_buffer_124_out, controlled_buffer_127_out, controlled_buffer_129_out,
       controlled_buffer_132_out, controlled_buffer_134_out, controlled_buffer_136_out,
       controlled_buffer_138_out, controlled_buffer_140_out, controlled_buffer_141_out,
       controlled_buffer_144_out, controlled_buffer_146_out, controlled_buffer_148_out,
       controlled_buffer_150_out, controlled_buffer_152_out, controlled_buffer_153_out,
       controlled_buffer_154_out, controlled_buffer_155_out, controlled_buffer_157_out,
       controlled_buffer_158_out, controlled_buffer_160_out, controlled_buffer_161_out,
       controlled_buffer_163_out, controlled_buffer_164_out, controlled_buffer_166_out,
       controlled_buffer_173_out, controlled_buffer_199_out, controlled_buffer_202_out,
       controlled_buffer_207_out, controlled_buffer_208_out, controlled_buffer_228_out,
       controlled_buffer_231_out, controlled_buffer_233_out, controlled_buffer_238_out,
       controlled_buffer_243_out, controlled_buffer_246_out, controlled_buffer_248_out,
       controlled_buffer_256_out, controlled_buffer_259_out, d_ff_1_q, d_ff_2_q, d_ff_3_q, d_ff_4_q,
       d_ff_5_q, d_ff_6_q, d_ff_7_q, d_ff_8_q, d_ff_9_q, d_ff_10_q, d_ff_11_q, d_ff_12_q, d_ff_13_q,
       d_ff_14_q, d_ff_15_q, d_ff_16_q, d_ff_17_q, d_ff_18_q, d_ff_19_q, d_ff_19_qn, d_ff_20_q, d_ff_21_q,
       d_ff_21_qn, d_ff_22_q, d_ff_23_q, d_ff_23_qn, d_ff_24_q, d_ff_25_qn, d_ff_26_q, d_ff_26_qn,
       d_ff_27_qn, d_ff_28_q, d_ff_29_q, d_ff_30_q, d_ff_31_q, d_ff_32_qn, d_ff_35_qn, d_ff_37_qn,
       d_ff_39_qn, d_ff_40_qn, d_ff_41_qn, d_ff_42_qn, d_ff_43_qn, d_ff_44_q, d_ff_45_q, d_ff_46_q,
       d_ff_46_qn, d_ff_47_q, d_ff_48_q, d_ff_49_q, d_ff_49_qn, d_ff_50_q, d_ff_51_q, d_ff_52_q, d_ff_52_qn,
       d_ff_53_q, d_ff_54_q, d_ff_54_qn, decoder_1_out0, decoder_1_out1, decoder_1_out2, decoder_1_out3,
       decoder_2_out0, decoder_2_out1, decoder_2_out2, decoder_2_out3, decoder_3_out0, decoder_3_out1,
       decoder_3_out2, decoder_3_out3, decoder_4_out0, decoder_4_out1, decoder_4_out2, decoder_4_out3,
       decoder_5_out0, decoder_5_out1, decoder_5_out2, decoder_5_out3, decoder_6_out1, decoder_6_out2,
       decoder_6_out3, decoder_6_out4, decoder_6_out5, decoder_6_out6, decoder_6_out7, decoder_6_out8,
       decoder_6_out9, decoder_6_out10, decoder_6_out11, decoder_6_out12, decoder_6_out13, decoder_6_out14,
       decoder_6_out15, nor_1_out, nor_2_out, nor_3_out, nor_4_out, nor_5_out, nor_6_out, not_1_out,
       not_2_out, not_3_out, not_4_out, not_5_out, not_6_out, not_7_out, not_8_out, not_9_out, not_10_out,
       not_11_out, not_12_out, not_13_out, not_14_out, not_15_out, not_16_out, not_17_out, not_18_out,
       not_19_out, not_20_out, not_21_out, not_22_out, not_23_out, not_24_out, not_25_out, not_26_out,
       not_27_out, not_28_out, not_29_out, not_30_out, not_31_out, not_32_out, not_33_out, not_34_out,
       or_1_out, or_2_out, or_3_out, or_4_out, or_5_out, or_6_out, or_7_out, or_8_out, or_9_out, or_10_out,
       or_11_out, or_12_out, or_13_out, or_14_out, or_15_out, or_16_out, or_17_out, or_18_out, or_19_out,
       or_20_out, por_1_out, pull_resistor_1_node, pull_resistor_2_node, pull_resistor_3_node,
       pull_resistor_4_node, pull_resistor_5_node, pull_resistor_6_node, pull_resistor_7_node,
       pull_resistor_8_node, pull_resistor_9_node, pull_resistor_10_node, pull_resistor_11_node,
       pull_resistor_12_node, pull_resistor_13_node, pull_resistor_14_node, pull_resistor_15_node,
       pull_resistor_16_node, pull_resistor_17_node, pull_resistor_18_node, pull_resistor_19_node,
       pull_resistor_20_node, pull_resistor_21_node, pull_resistor_26_node, pull_resistor_27_node,
       pull_resistor_28_node, pull_resistor_29_node, pull_resistor_30_node, pull_resistor_34_node,
       pull_resistor_35_node, pull_resistor_39_node, pull_resistor_49_node, pull_resistor_50_node,
       pull_resistor_52_node, pull_resistor_53_node, pull_resistor_64_node, pull_resistor_68_node,
       pull_resistor_69_node, pull_resistor_70_node, pull_resistor_71_node, pull_resistor_72_node,
       pull_resistor_73_node, pull_resistor_74_node, pull_resistor_75_node, pull_resistor_77_node,
       pull_resistor_78_node, pull_resistor_79_node, pull_resistor_80_node, pull_resistor_81_node,
       pull_resistor_82_node, pull_resistor_83_node, pull_resistor_89_node, pull_resistor_96_node,
       pull_resistor_97_node, pull_resistor_98_node, pull_resistor_99_node, pull_resistor_100_node,
       pull_resistor_101_node, pull_resistor_102_node, pull_resistor_103_node, pull_resistor_104_node,
       pull_resistor_105_node, pull_resistor_106_node, pull_resistor_107_node, pull_resistor_108_node,
       pull_resistor_109_node, pull_resistor_110_node, pull_resistor_111_node, pull_resistor_112_node,
       pull_resistor_113_node, pull_resistor_114_node, pull_resistor_115_node, pull_resistor_116_node,
       pull_resistor_117_node, pull_resistor_118_node, pull_resistor_119_node, pull_resistor_120_node,
       pull_resistor_122_node, pull_resistor_123_node, pull_resistor_124_node, pull_resistor_128_node,
       pull_resistor_132_node, xor_1_out, xor_2_out, xor_3_out, xor_4_out, xor_5_out, xor_6_out, xor_7_out,
       xor_8_out, xor_9_out, xor_10_out, xor_11_out, xor_12_out;
  wire [1:0] d_ff_25_q, pull_resistor_31_node, pull_resistor_32_node, pull_resistor_33_node,
       pull_resistor_48_node;
  wire [3:0] controlled_buffer_77_out, d_ff_33_q, ram_1_dout;
  wire [7:0] controlled_buffer_86_out, d_ff_32_q, rom_1_data;

  Decoder #(.select(2)) decoder_1 (
    .out0(decoder_1_out0), .out1(decoder_1_out1), .out2(decoder_1_out2), .out3(decoder_1_out3),
    .sel(pull_resistor_32_node));  // open: en
  Pull_Resistor pull_resistor_1 (.node(pull_resistor_1_node));
  Pull_Resistor pull_resistor_2 (.node(pull_resistor_2_node));
  assign pull_resistor_2_node = or_3_out ? decoder_1_out1 : 1'bz;  // Controlled_Buffer controlled_buffer_1
  assign pull_resistor_1_node = or_3_out ? decoder_1_out0 : 1'bz;  // Controlled_Buffer controlled_buffer_2
  Pull_Resistor pull_resistor_3 (.node(pull_resistor_3_node));
  Pull_Resistor pull_resistor_4 (.node(pull_resistor_4_node));
  assign pull_resistor_4_node = or_3_out ? decoder_1_out3 : 1'bz;  // Controlled_Buffer controlled_buffer_3
  assign pull_resistor_3_node = or_3_out ? decoder_1_out2 : 1'bz;  // Controlled_Buffer controlled_buffer_4
  Pull_Resistor pull_resistor_5 (.node(pull_resistor_5_node));
  assign pull_resistor_5_node = pull_resistor_1_node ? controlled_buffer_90_out : 1'bz;  // Controlled_Buffer controlled_buffer_5
  Pull_Resistor pull_resistor_6 (.node(pull_resistor_6_node));
  assign pull_resistor_6_node = pull_resistor_1_node ? controlled_buffer_89_out : 1'bz;  // Controlled_Buffer controlled_buffer_6
  Pull_Resistor pull_resistor_7 (.node(pull_resistor_7_node));
  assign pull_resistor_7_node = pull_resistor_1_node ? controlled_buffer_88_out : 1'bz;  // Controlled_Buffer controlled_buffer_7
  Pull_Resistor pull_resistor_8 (.node(pull_resistor_8_node));
  assign pull_resistor_8_node = pull_resistor_1_node ? controlled_buffer_87_out : 1'bz;  // Controlled_Buffer controlled_buffer_8
  Pull_Resistor pull_resistor_9 (.node(pull_resistor_9_node));
  assign pull_resistor_9_node = pull_resistor_2_node ? controlled_buffer_90_out : 1'bz;  // Controlled_Buffer controlled_buffer_9
  Pull_Resistor pull_resistor_10 (.node(pull_resistor_10_node));
  assign pull_resistor_10_node = pull_resistor_2_node ? controlled_buffer_89_out : 1'bz;  // Controlled_Buffer controlled_buffer_10
  Pull_Resistor pull_resistor_11 (.node(pull_resistor_11_node));
  assign pull_resistor_11_node = pull_resistor_2_node ? controlled_buffer_88_out : 1'bz;  // Controlled_Buffer controlled_buffer_11
  Pull_Resistor pull_resistor_12 (.node(pull_resistor_12_node));
  assign pull_resistor_12_node = pull_resistor_2_node ? controlled_buffer_87_out : 1'bz;  // Controlled_Buffer controlled_buffer_12
  Pull_Resistor pull_resistor_13 (.node(pull_resistor_13_node));
  assign pull_resistor_13_node = pull_resistor_3_node ? controlled_buffer_90_out : 1'bz;  // Controlled_Buffer controlled_buffer_13
  Pull_Resistor pull_resistor_14 (.node(pull_resistor_14_node));
  assign pull_resistor_14_node = pull_resistor_3_node ? controlled_buffer_89_out : 1'bz;  // Controlled_Buffer controlled_buffer_14
  Pull_Resistor pull_resistor_15 (.node(pull_resistor_15_node));
  assign pull_resistor_15_node = pull_resistor_3_node ? controlled_buffer_88_out : 1'bz;  // Controlled_Buffer controlled_buffer_15
  Pull_Resistor pull_resistor_16 (.node(pull_resistor_16_node));
  assign pull_resistor_16_node = pull_resistor_3_node ? controlled_buffer_87_out : 1'bz;  // Controlled_Buffer controlled_buffer_16
  Pull_Resistor pull_resistor_17 (.node(pull_resistor_17_node));
  assign pull_resistor_17_node = pull_resistor_4_node ? controlled_buffer_90_out : 1'bz;  // Controlled_Buffer controlled_buffer_17
  Pull_Resistor pull_resistor_18 (.node(pull_resistor_18_node));
  assign pull_resistor_18_node = pull_resistor_4_node ? controlled_buffer_89_out : 1'bz;  // Controlled_Buffer controlled_buffer_18
  Pull_Resistor pull_resistor_19 (.node(pull_resistor_19_node));
  assign pull_resistor_19_node = pull_resistor_4_node ? controlled_buffer_88_out : 1'bz;  // Controlled_Buffer controlled_buffer_19
  Pull_Resistor pull_resistor_20 (.node(pull_resistor_20_node));
  assign pull_resistor_20_node = pull_resistor_4_node ? controlled_buffer_87_out : 1'bz;  // Controlled_Buffer controlled_buffer_20
  Pull_Resistor pull_resistor_21 (.node(pull_resistor_21_node));
  assign pull_resistor_21_node = not_1_out ? and_1_out : 1'bz;  // Controlled_Buffer controlled_buffer_21
  not not_1 (not_1_out, or_1_out);
  and and_1 (and_1_out, d_ff_23_q, decoder_5_out3);
  D_Flip_Flop d_ff_1 (
    .D(pull_resistor_5_node), .clk(controlled_buffer_22_out), .Q(d_ff_1_q));  // open: Qn, preset, reset
  assign controlled_buffer_22_out = pull_resistor_1_node ? pull_resistor_21_node : 1'bz;  // Controlled_Buffer controlled_buffer_22
  D_Flip_Flop d_ff_2 (
    .D(pull_resistor_6_node), .clk(controlled_buffer_22_out), .Q(d_ff_2_q));  // open: Qn, preset, reset
  D_Flip_Flop d_ff_3 (
    .D(pull_resistor_7_node), .clk(controlled_buffer_22_out), .Q(d_ff_3_q));  // open: Qn, preset, reset
  D_Flip_Flop d_ff_4 (
    .D(pull_resistor_8_node), .clk(controlled_buffer_22_out), .Q(d_ff_4_q));  // open: Qn, preset, reset
  Pull_Resistor pull_resistor_22 (.node(controlled_buffer_22_out));
  D_Flip_Flop d_ff_5 (
    .D(pull_resistor_9_node), .clk(controlled_buffer_23_out), .Q(d_ff_5_q));  // open: Qn, preset, reset
  assign controlled_buffer_23_out = pull_resistor_2_node ? pull_resistor_21_node : 1'bz;  // Controlled_Buffer controlled_buffer_23
  D_Flip_Flop d_ff_6 (
    .D(pull_resistor_10_node), .clk(controlled_buffer_23_out), .Q(d_ff_6_q));  // open: Qn, preset, reset
  D_Flip_Flop d_ff_7 (
    .D(pull_resistor_11_node), .clk(controlled_buffer_23_out), .Q(d_ff_7_q));  // open: Qn, preset, reset
  D_Flip_Flop d_ff_8 (
    .D(pull_resistor_12_node), .clk(controlled_buffer_23_out), .Q(d_ff_8_q));  // open: Qn, preset, reset
  Pull_Resistor pull_resistor_23 (.node(controlled_buffer_23_out));
  D_Flip_Flop d_ff_9 (
    .D(pull_resistor_13_node), .clk(controlled_buffer_24_out), .Q(d_ff_9_q));  // open: Qn, preset, reset
  assign controlled_buffer_24_out = pull_resistor_3_node ? pull_resistor_21_node : 1'bz;  // Controlled_Buffer controlled_buffer_24
  D_Flip_Flop d_ff_10 (
    .D(pull_resistor_14_node), .clk(controlled_buffer_24_out), .Q(d_ff_10_q));  // open: Qn, preset, reset
  D_Flip_Flop d_ff_11 (
    .D(pull_resistor_15_node), .clk(controlled_buffer_24_out), .Q(d_ff_11_q));  // open: Qn, preset, reset
  D_Flip_Flop d_ff_12 (
    .D(pull_resistor_16_node), .clk(controlled_buffer_24_out), .Q(d_ff_12_q));  // open: Qn, preset, reset
  Pull_Resistor pull_resistor_24 (.node(controlled_buffer_24_out));
  D_Flip_Flop d_ff_13 (
    .D(pull_resistor_17_node), .clk(controlled_buffer_25_out), .Q(d_ff_13_q));  // open: Qn, preset, reset
  assign controlled_buffer_25_out = pull_resistor_4_node ? pull_resistor_21_node : 1'bz;  // Controlled_Buffer controlled_buffer_25
  D_Flip_Flop d_ff_14 (
    .D(pull_resistor_18_node), .clk(controlled_buffer_25_out), .Q(d_ff_14_q));  // open: Qn, preset, reset
  D_Flip_Flop d_ff_15 (
    .D(pull_resistor_19_node), .clk(controlled_buffer_25_out), .Q(d_ff_15_q));  // open: Qn, preset, reset
  D_Flip_Flop d_ff_16 (
    .D(pull_resistor_20_node), .clk(controlled_buffer_25_out), .Q(d_ff_16_q));  // open: Qn, preset, reset
  Pull_Resistor pull_resistor_25 (.node(controlled_buffer_25_out));
  assign controlled_buffer_26_out = pull_resistor_34_node ? d_ff_1_q : 1'bz;  // Controlled_Buffer controlled_buffer_26
  assign controlled_buffer_27_out = pull_resistor_39_node ? d_ff_1_q : 1'bz;  // Controlled_Buffer controlled_buffer_27
  assign controlled_buffer_28_out = pull_resistor_34_node ? d_ff_2_q : 1'bz;  // Controlled_Buffer controlled_buffer_28
  assign controlled_buffer_29_out = pull_resistor_39_node ? d_ff_2_q : 1'bz;  // Controlled_Buffer controlled_buffer_29
  assign controlled_buffer_30_out = pull_resistor_34_node ? d_ff_3_q : 1'bz;  // Controlled_Buffer controlled_buffer_30
  assign controlled_buffer_31_out = pull_resistor_39_node ? d_ff_3_q : 1'bz;  // Controlled_Buffer controlled_buffer_31
  assign controlled_buffer_32_out = pull_resistor_34_node ? d_ff_4_q : 1'bz;  // Controlled_Buffer controlled_buffer_32
  assign controlled_buffer_33_out = pull_resistor_39_node ? d_ff_4_q : 1'bz;  // Controlled_Buffer controlled_buffer_33
  assign controlled_buffer_26_out = pull_resistor_29_node ? d_ff_5_q : 1'bz;  // Controlled_Buffer controlled_buffer_34
  assign controlled_buffer_27_out = pull_resistor_35_node ? d_ff_5_q : 1'bz;  // Controlled_Buffer controlled_buffer_35
  assign controlled_buffer_28_out = pull_resistor_29_node ? d_ff_6_q : 1'bz;  // Controlled_Buffer controlled_buffer_36
  assign controlled_buffer_29_out = pull_resistor_35_node ? d_ff_6_q : 1'bz;  // Controlled_Buffer controlled_buffer_37
  assign controlled_buffer_30_out = pull_resistor_29_node ? d_ff_7_q : 1'bz;  // Controlled_Buffer controlled_buffer_38
  assign controlled_buffer_31_out = pull_resistor_35_node ? d_ff_7_q : 1'bz;  // Controlled_Buffer controlled_buffer_39
  assign controlled_buffer_32_out = pull_resistor_29_node ? d_ff_8_q : 1'bz;  // Controlled_Buffer controlled_buffer_40
  assign controlled_buffer_33_out = pull_resistor_35_node ? d_ff_8_q : 1'bz;  // Controlled_Buffer controlled_buffer_41
  assign controlled_buffer_26_out = pull_resistor_27_node ? d_ff_9_q : 1'bz;  // Controlled_Buffer controlled_buffer_42
  assign controlled_buffer_27_out = pull_resistor_30_node ? d_ff_9_q : 1'bz;  // Controlled_Buffer controlled_buffer_43
  assign controlled_buffer_28_out = pull_resistor_27_node ? d_ff_10_q : 1'bz;  // Controlled_Buffer controlled_buffer_44
  assign controlled_buffer_29_out = pull_resistor_30_node ? d_ff_10_q : 1'bz;  // Controlled_Buffer controlled_buffer_45
  assign controlled_buffer_30_out = pull_resistor_27_node ? d_ff_11_q : 1'bz;  // Controlled_Buffer controlled_buffer_46
  assign controlled_buffer_31_out = pull_resistor_30_node ? d_ff_11_q : 1'bz;  // Controlled_Buffer controlled_buffer_47
  assign controlled_buffer_32_out = pull_resistor_27_node ? d_ff_12_q : 1'bz;  // Controlled_Buffer controlled_buffer_48
  assign controlled_buffer_33_out = pull_resistor_30_node ? d_ff_12_q : 1'bz;  // Controlled_Buffer controlled_buffer_49
  assign controlled_buffer_26_out = pull_resistor_26_node ? d_ff_13_q : 1'bz;  // Controlled_Buffer controlled_buffer_50
  assign controlled_buffer_27_out = pull_resistor_28_node ? d_ff_13_q : 1'bz;  // Controlled_Buffer controlled_buffer_51
  assign controlled_buffer_28_out = pull_resistor_26_node ? d_ff_14_q : 1'bz;  // Controlled_Buffer controlled_buffer_52
  assign controlled_buffer_29_out = pull_resistor_28_node ? d_ff_14_q : 1'bz;  // Controlled_Buffer controlled_buffer_53
  assign controlled_buffer_30_out = pull_resistor_26_node ? d_ff_15_q : 1'bz;  // Controlled_Buffer controlled_buffer_54
  assign controlled_buffer_31_out = pull_resistor_28_node ? d_ff_15_q : 1'bz;  // Controlled_Buffer controlled_buffer_55
  assign controlled_buffer_32_out = pull_resistor_26_node ? d_ff_16_q : 1'bz;  // Controlled_Buffer controlled_buffer_56
  assign controlled_buffer_33_out = pull_resistor_28_node ? d_ff_16_q : 1'bz;  // Controlled_Buffer controlled_buffer_57
  Decoder #(.select(2)) decoder_2 (
    .out0(decoder_2_out0), .out1(decoder_2_out1), .out2(decoder_2_out2), .out3(decoder_2_out3),
    .sel(pull_resistor_31_node));  // open: en
  Decoder #(.select(2)) decoder_3 (
    .out0(decoder_3_out0), .out1(decoder_3_out1), .out2(decoder_3_out2), .out3(decoder_3_out3),
    .sel(pull_resistor_33_node));  // open: en
  Pull_Resistor pull_resistor_26 (.node(pull_resistor_26_node));
  Pull_Resistor pull_resistor_27 (.node(pull_resistor_27_node));
  assign pull_resistor_26_node = or_3_out ? decoder_2_out3 : 1'bz;  // Controlled_Buffer controlled_buffer_58
  assign pull_resistor_27_node = or_3_out ? decoder_2_out2 : 1'bz;  // Controlled_Buffer controlled_buffer_59
  Pull_Resistor pull_resistor_28 (.node(pull_resistor_28_node));
  assign pull_resistor_28_node = or_3_out ? decoder_3_out3 : 1'bz;  // Controlled_Buffer controlled_buffer_60
  Pull_Resistor pull_resistor_29 (.node(pull_resistor_29_node));
  assign pull_resistor_29_node = or_3_out ? decoder_2_out1 : 1'bz;  // Controlled_Buffer controlled_buffer_61
  Pull_Resistor pull_resistor_30 (.node(pull_resistor_30_node));
  assign pull_resistor_30_node = or_3_out ? decoder_3_out2 : 1'bz;  // Controlled_Buffer controlled_buffer_62
  Pull_Resistor pull_resistor_31 (.node(pull_resistor_31_node[0]));
  Pull_Resistor pull_resistor_32 (.node(pull_resistor_32_node[0]));
  Pull_Resistor pull_resistor_33 (.node(pull_resistor_33_node[0]));
  Pull_Resistor pull_resistor_34 (.node(pull_resistor_34_node));
  assign pull_resistor_34_node = or_3_out ? decoder_2_out0 : 1'bz;  // Controlled_Buffer controlled_buffer_63
  Pull_Resistor pull_resistor_35 (.node(pull_resistor_35_node));
  assign pull_resistor_35_node = or_3_out ? decoder_3_out1 : 1'bz;  // Controlled_Buffer controlled_buffer_64
  Pull_Resistor pull_resistor_36 (.node(pull_resistor_31_node[1]));
  Pull_Resistor pull_resistor_37 (.node(pull_resistor_32_node[1]));
  Pull_Resistor pull_resistor_38 (.node(pull_resistor_33_node[1]));
  Pull_Resistor pull_resistor_39 (.node(pull_resistor_39_node));
  assign pull_resistor_39_node = or_3_out ? decoder_3_out0 : 1'bz;  // Controlled_Buffer controlled_buffer_65
  Pull_Resistor pull_resistor_40 (.node(controlled_buffer_26_out));
  Pull_Resistor pull_resistor_41 (.node(controlled_buffer_28_out));
  Pull_Resistor pull_resistor_42 (.node(controlled_buffer_30_out));
  Pull_Resistor pull_resistor_43 (.node(controlled_buffer_32_out));
  Pull_Resistor pull_resistor_44 (.node(controlled_buffer_27_out));
  Pull_Resistor pull_resistor_45 (.node(controlled_buffer_29_out));
  Pull_Resistor pull_resistor_46 (.node(controlled_buffer_31_out));
  Pull_Resistor pull_resistor_47 (.node(controlled_buffer_33_out));
  Pull_Resistor pull_resistor_48 (.node(pull_resistor_48_node[0]));
  Decoder #(.select(2)) decoder_4 (
    .out0(decoder_4_out0), .out1(decoder_4_out1), .out2(decoder_4_out2), .out3(decoder_4_out3),
    .sel(pull_resistor_48_node));  // open: en
  nor nor_1 (nor_1_out, d_ff_1_q, d_ff_2_q, d_ff_3_q, d_ff_4_q);
  assign controlled_buffer_66_out = pull_resistor_50_node ? nor_1_out : 1'bz;  // Controlled_Buffer controlled_buffer_66
  nor nor_2 (nor_2_out, d_ff_5_q, d_ff_6_q, d_ff_7_q, d_ff_8_q);
  nor nor_3 (nor_3_out, d_ff_9_q, d_ff_10_q, d_ff_11_q, d_ff_12_q);
  nor nor_4 (nor_4_out, d_ff_13_q, d_ff_14_q, d_ff_15_q, d_ff_16_q);
  Pull_Resistor pull_resistor_49 (.node(pull_resistor_49_node));
  Pull_Resistor pull_resistor_50 (.node(pull_resistor_50_node));
  assign pull_resistor_49_node = decoder_6_out14 ? decoder_4_out1 : 1'bz;  // Controlled_Buffer controlled_buffer_67
  assign pull_resistor_50_node = decoder_6_out14 ? decoder_4_out0 : 1'bz;  // Controlled_Buffer controlled_buffer_68
  Pull_Resistor pull_resistor_51 (.node(pull_resistor_48_node[1]));
  assign pull_resistor_48_node[1] = decoder_6_out14 ? d_ff_31_q : 1'bz;  // Controlled_Buffer controlled_buffer_69
  assign pull_resistor_48_node[0] = decoder_6_out14 ? d_ff_30_q : 1'bz;  // Controlled_Buffer controlled_buffer_70
  assign pull_resistor_31_node[1] = or_3_out ? d_ff_31_q : 1'bz;  // Controlled_Buffer controlled_buffer_71
  assign pull_resistor_31_node[0] = or_3_out ? d_ff_30_q : 1'bz;  // Controlled_Buffer controlled_buffer_72
  assign pull_resistor_32_node[1] = or_3_out ? d_ff_31_q : 1'bz;  // Controlled_Buffer controlled_buffer_73
  assign pull_resistor_32_node[0] = or_3_out ? d_ff_30_q : 1'bz;  // Controlled_Buffer controlled_buffer_74
  assign pull_resistor_33_node[1] = or_3_out ? d_ff_29_q : 1'bz;  // Controlled_Buffer controlled_buffer_75
  assign pull_resistor_33_node[0] = or_3_out ? d_ff_28_q : 1'bz;  // Controlled_Buffer controlled_buffer_76
  assign controlled_buffer_77_out[0] = decoder_6_out2 ? controlled_buffer_33_out : 1'bz;  // Controlled_Buffer controlled_buffer_77
  assign controlled_buffer_66_out = pull_resistor_49_node ? nor_2_out : 1'bz;  // Controlled_Buffer controlled_buffer_78
  assign controlled_buffer_66_out = pull_resistor_53_node ? nor_3_out : 1'bz;  // Controlled_Buffer controlled_buffer_79
  assign controlled_buffer_66_out = pull_resistor_52_node ? nor_4_out : 1'bz;  // Controlled_Buffer controlled_buffer_80
  Pull_Resistor pull_resistor_52 (.node(pull_resistor_52_node));
  Pull_Resistor pull_resistor_53 (.node(pull_resistor_53_node));
  assign pull_resistor_52_node = decoder_6_out14 ? decoder_4_out3 : 1'bz;  // Controlled_Buffer controlled_buffer_81
  assign pull_resistor_53_node = decoder_6_out14 ? decoder_4_out2 : 1'bz;  // Controlled_Buffer controlled_buffer_82
  Pull_Resistor pull_resistor_54 (.node(controlled_buffer_77_out[0]));
  assign controlled_buffer_77_out[1] = decoder_6_out2 ? controlled_buffer_31_out : 1'bz;  // Controlled_Buffer controlled_buffer_83
  LED led_1 (.in(controlled_buffer_66_out));
  Pull_Resistor pull_resistor_55 (.node(controlled_buffer_66_out));
  Pull_Resistor pull_resistor_56 (.node(controlled_buffer_77_out[1]));
  Pull_Resistor pull_resistor_57 (.node(controlled_buffer_77_out[2]));
  assign controlled_buffer_77_out[2] = decoder_6_out2 ? controlled_buffer_29_out : 1'bz;  // Controlled_Buffer controlled_buffer_84
  or or_1 (or_1_out, decoder_6_out1, decoder_6_out2);
  or or_2 (or_2_out, decoder_6_out1, and_2_out);
  Pull_Resistor pull_resistor_58 (.node(controlled_buffer_77_out[3]));
  assign controlled_buffer_77_out[3] = decoder_6_out2 ? controlled_buffer_27_out : 1'bz;  // Controlled_Buffer controlled_buffer_85
  or or_3 (or_3_out, decoder_6_out1, decoder_6_out2, decoder_6_out3, decoder_6_out4, decoder_6_out5, decoder_6_out6, decoder_6_out7, decoder_6_out8, decoder_6_out9, decoder_6_out10, decoder_6_out11, decoder_6_out12);
  assign controlled_buffer_86_out = or_2_out ? rom_1_data : 8'bz;  // Controlled_Buffer controlled_buffer_86
  Pull_Resistor pull_resistor_59 (.node(controlled_buffer_86_out));
  and and_2 (and_2_out, decoder_6_out2, d_ff_19_q);
  RAM #(.dataWidth(4)) ram_1 (
    .addr(controlled_buffer_86_out), .we(and_2_out), .oe(decoder_6_out1), .clk(and_3_out),
    .din(controlled_buffer_77_out), .dout(ram_1_dout));
  and and_3 (and_3_out, clock_1_out, decoder_5_out3, not_2_out);
  D_Flip_Flop #(.trigger("falling")) d_ff_17 (
    .D(or_4_out), .clk(clock_1_out), .Q(d_ff_17_q));  // open: Qn, preset, reset
  not not_2 (not_2_out, d_ff_23_q);
  assign controlled_buffer_87_out = decoder_6_out1 ? ram_1_dout[0] : 1'bz;  // Controlled_Buffer controlled_buffer_87
  Pull_Resistor pull_resistor_60 (.node(ram_1_dout[0]));
  and and_4 (and_4_out, or_4_out, not_3_out);
  not not_3 (not_3_out, d_ff_17_q);
  D_Flip_Flop #(.trigger("falling")) d_ff_18 (
    .D(and_4_out), .clk(clock_1_out), .Q(d_ff_18_q));  // open: Qn, preset, reset
  assign controlled_buffer_88_out = decoder_6_out1 ? ram_1_dout[1] : 1'bz;  // Controlled_Buffer controlled_buffer_88
  Pull_Resistor pull_resistor_61 (.node(ram_1_dout[1]));
  Pull_Resistor pull_resistor_62 (.node(ram_1_dout[2]));
  not not_4 (not_4_out, d_ff_47_q);
  and and_5 (and_5_out, decoder_6_out15, not_4_out);
  or or_4 (or_4_out, and_5_out, and_6_out);
  assign controlled_buffer_89_out = decoder_6_out1 ? ram_1_dout[2] : 1'bz;  // Controlled_Buffer controlled_buffer_89
  assign controlled_buffer_90_out = decoder_6_out1 ? ram_1_dout[3] : 1'bz;  // Controlled_Buffer controlled_buffer_90
  Pull_Resistor pull_resistor_63 (.node(ram_1_dout[3]));
  D_Flip_Flop #(.trigger("falling")) d_ff_19 (
    .D(d_ff_19_qn), .clk(pull_resistor_70_node), .Q(d_ff_19_q), .Qn(d_ff_19_qn));  // open: preset, reset
  not not_5 (not_5_out, controlled_buffer_66_out);
  and and_6 (and_6_out, decoder_6_out14, not_5_out);
  Pull_Resistor pull_resistor_64 (.node(pull_resistor_64_node));
  and and_7 (and_7_out, d_ff_23_q, decoder_5_out0);
  assign pull_resistor_64_node = and_13_out ? and_8_out : 1'bz;  // Controlled_Buffer controlled_buffer_91
  and and_8 (and_8_out, not_2_out, not_6_out, decoder_5_out1);
  and and_9 (and_9_out, d_ff_23_q, decoder_5_out1);
  not not_6 (not_6_out, clock_1_out);
  POR #(.porsize(1)) por_1 (.out(por_1_out));
  assign controlled_buffer_87_out = decoder_6_out12 ? controlled_buffer_33_out : 1'bz;  // Controlled_Buffer controlled_buffer_92
  assign controlled_buffer_93_out = decoder_6_out14 ? controlled_buffer_66_out : 1'bz;  // Controlled_Buffer controlled_buffer_93
  Pull_Resistor pull_resistor_65 (.node(controlled_buffer_93_out));
  assign controlled_buffer_94_out = decoder_6_out15 ? d_ff_47_q : 1'bz;  // Controlled_Buffer controlled_buffer_94
  Pull_Resistor pull_resistor_66 (.node(controlled_buffer_94_out));
  or or_5 (or_5_out, controlled_buffer_94_out, controlled_buffer_93_out, decoder_6_out13);
  D_Flip_Flop #(.trigger("falling")) d_ff_20 (
    .D(or_5_out), .clk(and_7_out), .Q(d_ff_20_q), .reset(pull_resistor_64_node));  // open: Qn, preset
  assign controlled_buffer_95_out = not_7_out ? and_7_out : 1'bz;  // Controlled_Buffer controlled_buffer_95
  not not_7 (not_7_out, and_11_out);
  Pull_Resistor pull_resistor_67 (.node(controlled_buffer_95_out));
  D_Flip_Flop #(.trigger("falling")) d_ff_21 (
    .D(d_ff_21_qn), .clk(pull_resistor_68_node), .Q(d_ff_21_q), .Qn(d_ff_21_qn), .reset(not_12_out));  // open: preset
  Pull_Resistor pull_resistor_68 (.node(pull_resistor_68_node));
  assign pull_resistor_68_node = d_ff_21_qn ? and_9_out : 1'bz;  // Controlled_Buffer controlled_buffer_96
  Clock clock_1 (.out(clock_1_out));
  assign controlled_buffer_88_out = decoder_6_out12 ? controlled_buffer_31_out : 1'bz;  // Controlled_Buffer controlled_buffer_97
  D_Flip_Flop #(.trigger("falling")) d_ff_22 (
    .D(or_7_out), .clk(d_ff_19_q), .Q(d_ff_22_q), .reset(and_10_out));  // open: Qn, preset
  and and_10 (and_10_out, not_8_out, decoder_5_out2);
  not not_8 (not_8_out, d_ff_19_q);
  and and_11 (and_11_out, or_5_out, not_9_out);
  not not_9 (not_9_out, d_ff_20_q);
  or or_6 (or_6_out, por_1_out, controlled_buffer_95_out);
  Pull_Resistor pull_resistor_69 (.node(pull_resistor_69_node));
  assign pull_resistor_69_node = d_ff_21_q ? and_9_out : 1'bz;  // Controlled_Buffer controlled_buffer_98
  D_Flip_Flop #(.trigger("falling")) d_ff_23 (
    .D(d_ff_23_qn), .clk(clock_1_out), .Q(d_ff_23_q), .Qn(d_ff_23_qn));  // open: preset, reset
  assign controlled_buffer_89_out = decoder_6_out12 ? controlled_buffer_29_out : 1'bz;  // Controlled_Buffer controlled_buffer_99
  or or_7 (or_7_out, decoder_6_out2, decoder_6_out1, decoder_6_out11);
  and and_12 (and_12_out, or_7_out, not_10_out);
  not not_10 (not_10_out, d_ff_22_q);
  Pull_Resistor pull_resistor_70 (.node(pull_resistor_70_node));
  assign pull_resistor_70_node = and_12_out ? and_14_out : 1'bz;  // Controlled_Buffer controlled_buffer_100
  not not_11 (not_11_out, or_5_out);
  nor nor_5 (nor_5_out, and_11_out, nor_6_out);
  nor nor_6 (nor_6_out, nor_5_out, or_6_out);
  D_Flip_Flop d_ff_24 (
    .D(nor_6_out), .clk(pull_resistor_69_node), .Q(d_ff_24_q), .reset(not_12_out));  // open: Qn, preset
  not not_12 (not_12_out, nor_6_out);
  Pull_Resistor pull_resistor_71 (.node(pull_resistor_71_node));
  assign pull_resistor_71_node = d_ff_26_qn ? decoder_5_out0 : 1'bz;  // Controlled_Buffer controlled_buffer_101
  D_Flip_Flop #(.trigger("falling")) d_ff_25 (
    .D(d_ff_25_qn), .clk(d_ff_23_q), .Q(d_ff_25_q[0]), .Qn(d_ff_25_qn));  // open: preset, reset
  assign controlled_buffer_90_out = decoder_6_out12 ? controlled_buffer_27_out : 1'bz;  // Controlled_Buffer controlled_buffer_102
  not not_13 (not_13_out, and_12_out);
  assign controlled_buffer_103_out = not_11_out ? not_13_out : 1'bz;  // Controlled_Buffer controlled_buffer_103
  assign controlled_buffer_103_out = or_5_out ? nor_5_out : 1'bz;  // Controlled_Buffer controlled_buffer_104
  and and_13 (and_13_out, or_5_out, nor_5_out);
  or or_8 (or_8_out, d_ff_24_q, por_1_out);
  D_Flip_Flop #(.trigger("falling")) d_ff_26 (
    .D(d_ff_26_qn), .clk(pull_resistor_71_node), .Q(d_ff_26_q), .Qn(d_ff_26_qn), .reset(or_8_out));  // open: preset
  D_Flip_Flop #(.trigger("falling")) d_ff_27 (
    .D(d_ff_27_qn), .clk(d_ff_25_q[0]), .Q(d_ff_25_q[1]), .Qn(d_ff_27_qn));  // open: preset, reset
  assign controlled_buffer_88_out = decoder_6_out11 ? rom_1_data[1] : 1'bz;  // Controlled_Buffer controlled_buffer_105
  assign controlled_buffer_87_out = decoder_6_out11 ? rom_1_data[0] : 1'bz;  // Controlled_Buffer controlled_buffer_106
  and and_14 (and_14_out, d_ff_23_q, decoder_5_out0);
  Pull_Resistor pull_resistor_72 (.node(pull_resistor_72_node));
  assign pull_resistor_72_node = d_ff_26_q ? decoder_5_out0 : 1'bz;  // Controlled_Buffer controlled_buffer_107
  Decoder #(.select(2)) decoder_5 (
    .out0(decoder_5_out0), .out1(decoder_5_out1), .out2(decoder_5_out2), .out3(decoder_5_out3),
    .sel(d_ff_25_q));  // open: en
  assign controlled_buffer_90_out = decoder_6_out11 ? rom_1_data[3] : 1'bz;  // Controlled_Buffer controlled_buffer_108
  assign controlled_buffer_89_out = decoder_6_out11 ? rom_1_data[2] : 1'bz;  // Controlled_Buffer controlled_buffer_109
  Pull_Resistor pull_resistor_73 (.node(pull_resistor_73_node));
  not not_14 (not_14_out, or_8_out);
  Pull_Resistor pull_resistor_74 (.node(pull_resistor_74_node));
  assign pull_resistor_74_node = pull_resistor_75_node ? rom_1_data[0] : 1'bz;  // Controlled_Buffer controlled_buffer_110
  and and_15 (and_15_out, pull_resistor_73_node, decoder_5_out1);
  Pull_Resistor pull_resistor_75 (.node(pull_resistor_75_node));
  assign pull_resistor_73_node = controlled_buffer_103_out ? d_ff_23_q : 1'bz;  // Controlled_Buffer controlled_buffer_111
  assign pull_resistor_75_node = controlled_buffer_103_out ? not_14_out : 1'bz;  // Controlled_Buffer controlled_buffer_112
  D_Flip_Flop d_ff_28 (
    .D(pull_resistor_74_node), .clk(and_15_out), .Q(d_ff_28_q), .reset(pull_resistor_64_node));  // open: Qn, preset
  Pull_Resistor pull_resistor_76 (.node(or_8_out));
  and and_16 (and_16_out, pull_resistor_72_node, d_ff_23_q);
  D_Flip_Flop d_ff_29 (
    .D(pull_resistor_77_node), .clk(and_15_out), .Q(d_ff_29_q), .reset(pull_resistor_64_node));  // open: Qn, preset
  Pull_Resistor pull_resistor_77 (.node(pull_resistor_77_node));
  assign pull_resistor_77_node = pull_resistor_75_node ? rom_1_data[1] : 1'bz;  // Controlled_Buffer controlled_buffer_113
  or or_9 (or_9_out, and_16_out, d_ff_18_q);
  Pull_Resistor pull_resistor_78 (.node(pull_resistor_78_node));
  assign pull_resistor_78_node = pull_resistor_75_node ? rom_1_data[2] : 1'bz;  // Controlled_Buffer controlled_buffer_114
  ROM rom_1 (.addr(d_ff_32_q), .data(rom_1_data));
  Decoder #(.select(4)) decoder_6 (
    .out1(decoder_6_out1), .out2(decoder_6_out2), .out3(decoder_6_out3), .out4(decoder_6_out4),
    .out5(decoder_6_out5), .out6(decoder_6_out6), .out7(decoder_6_out7), .out8(decoder_6_out8),
    .out9(decoder_6_out9), .out10(decoder_6_out10), .out11(decoder_6_out11), .out12(decoder_6_out12),
    .out13(decoder_6_out13), .out14(decoder_6_out14), .out15(decoder_6_out15), .sel(d_ff_33_q));  // open: out0, en
  D_Flip_Flop d_ff_30 (
    .D(pull_resistor_78_node), .clk(and_15_out), .Q(d_ff_30_q), .reset(pull_resistor_64_node));  // open: Qn, preset
  assign controlled_buffer_115_out = not_14_out ? d_ff_32_qn : 1'bz;  // Controlled_Buffer controlled_buffer_115
  D_Flip_Flop d_ff_31 (
    .D(pull_resistor_79_node), .clk(and_15_out), .Q(d_ff_31_q), .reset(pull_resistor_64_node));  // open: Qn, preset
  Pull_Resistor pull_resistor_79 (.node(pull_resistor_79_node));
  assign pull_resistor_79_node = pull_resistor_75_node ? rom_1_data[3] : 1'bz;  // Controlled_Buffer controlled_buffer_116
  assign controlled_buffer_115_out = or_8_out ? rom_1_data[0] : 1'bz;  // Controlled_Buffer controlled_buffer_117
  D_Flip_Flop #(.trigger("falling")) d_ff_32 (
    .D(controlled_buffer_115_out), .clk(controlled_buffer_118_out), .Q(d_ff_32_q[0]), .Qn(d_ff_32_qn));  // open: preset, reset
  assign controlled_buffer_118_out = not_14_out ? or_9_out : 1'bz;  // Controlled_Buffer controlled_buffer_118
  assign controlled_buffer_118_out = or_8_out ? decoder_5_out1 : 1'bz;  // Controlled_Buffer controlled_buffer_119
  D_Flip_Flop d_ff_33 (
    .D(pull_resistor_80_node), .clk(and_15_out), .Q(d_ff_33_q[0]), .reset(pull_resistor_64_node));  // open: Qn, preset
  Pull_Resistor pull_resistor_80 (.node(pull_resistor_80_node));
  assign pull_resistor_80_node = pull_resistor_75_node ? rom_1_data[4] : 1'bz;  // Controlled_Buffer controlled_buffer_120
  Pull_Resistor pull_resistor_81 (.node(pull_resistor_81_node));
  assign pull_resistor_81_node = pull_resistor_75_node ? rom_1_data[5] : 1'bz;  // Controlled_Buffer controlled_buffer_121
  assign controlled_buffer_122_out = or_8_out ? rom_1_data[1] : 1'bz;  // Controlled_Buffer controlled_buffer_122
  assign controlled_buffer_122_out = not_14_out ? d_ff_35_qn : 1'bz;  // Controlled_Buffer controlled_buffer_123
  assign controlled_buffer_124_out = not_14_out ? d_ff_32_q[0] : 1'bz;  // Controlled_Buffer controlled_buffer_124
  assign controlled_buffer_124_out = or_8_out ? controlled_buffer_118_out : 1'bz;  // Controlled_Buffer controlled_buffer_125
  D_Flip_Flop d_ff_34 (
    .D(pull_resistor_81_node), .clk(and_15_out), .Q(d_ff_33_q[1]), .reset(pull_resistor_64_node));  // open: Qn, preset
  D_Flip_Flop #(.trigger("falling")) d_ff_35 (
    .D(controlled_buffer_122_out), .clk(controlled_buffer_124_out), .Q(d_ff_32_q[1]), .Qn(d_ff_35_qn));  // open: preset, reset
  D_Flip_Flop d_ff_36 (
    .D(pull_resistor_82_node), .clk(and_15_out), .Q(d_ff_33_q[2]), .reset(pull_resistor_64_node));  // open: Qn, preset
  Pull_Resistor pull_resistor_82 (.node(pull_resistor_82_node));
  assign pull_resistor_82_node = pull_resistor_75_node ? rom_1_data[6] : 1'bz;  // Controlled_Buffer controlled_buffer_126
  assign controlled_buffer_127_out = or_8_out ? rom_1_data[2] : 1'bz;  // Controlled_Buffer controlled_buffer_127
  assign controlled_buffer_127_out = not_14_out ? d_ff_37_qn : 1'bz;  // Controlled_Buffer controlled_buffer_128
  assign controlled_buffer_129_out = not_14_out ? d_ff_32_q[1] : 1'bz;  // Controlled_Buffer controlled_buffer_129
  assign controlled_buffer_129_out = or_8_out ? controlled_buffer_124_out : 1'bz;  // Controlled_Buffer controlled_buffer_130
  Pull_Resistor pull_resistor_83 (.node(pull_resistor_83_node));
  assign pull_resistor_83_node = pull_resistor_75_node ? rom_1_data[7] : 1'bz;  // Controlled_Buffer controlled_buffer_131
  D_Flip_Flop #(.trigger("falling")) d_ff_37 (
    .D(controlled_buffer_127_out), .clk(controlled_buffer_129_out), .Q(d_ff_32_q[2]), .Qn(d_ff_37_qn));  // open: preset, reset
  D_Flip_Flop d_ff_38 (
    .D(pull_resistor_83_node), .clk(and_15_out), .Q(d_ff_33_q[3]), .reset(pull_resistor_64_node));  // open: Qn, preset
  assign controlled_buffer_132_out = not_14_out ? d_ff_39_qn : 1'bz;  // Controlled_Buffer controlled_buffer_132
  assign controlled_buffer_132_out = or_8_out ? rom_1_data[3] : 1'bz;  // Controlled_Buffer controlled_buffer_133
  D_Flip_Flop #(.trigger("falling")) d_ff_39 (
    .D(controlled_buffer_132_out), .clk(controlled_buffer_134_out), .Q(d_ff_32_q[3]), .Qn(d_ff_39_qn));  // open: preset, reset
  assign controlled_buffer_134_out = not_14_out ? d_ff_32_q[2] : 1'bz;  // Controlled_Buffer controlled_buffer_134
  assign controlled_buffer_134_out = or_8_out ? controlled_buffer_129_out : 1'bz;  // Controlled_Buffer controlled_buffer_135
  assign controlled_buffer_136_out = or_8_out ? rom_1_data[4] : 1'bz;  // Controlled_Buffer controlled_buffer_136
  assign controlled_buffer_136_out = not_14_out ? d_ff_40_qn : 1'bz;  // Controlled_Buffer controlled_buffer_137
  assign controlled_buffer_138_out = not_14_out ? d_ff_32_q[3] : 1'bz;  // Controlled_Buffer controlled_buffer_138
  assign controlled_buffer_138_out = or_8_out ? controlled_buffer_134_out : 1'bz;  // Controlled_Buffer controlled_buffer_139
  D_Flip_Flop #(.trigger("falling")) d_ff_40 (
    .D(controlled_buffer_136_out), .clk(controlled_buffer_138_out), .Q(d_ff_32_q[4]), .Qn(d_ff_40_qn));  // open: preset, reset
  assign controlled_buffer_140_out = not_14_out ? d_ff_41_qn : 1'bz;  // Controlled_Buffer controlled_buffer_140
  assign controlled_buffer_141_out = not_14_out ? d_ff_32_q[4] : 1'bz;  // Controlled_Buffer controlled_buffer_141
  assign controlled_buffer_141_out = or_8_out ? controlled_buffer_138_out : 1'bz;  // Controlled_Buffer controlled_buffer_142
  assign controlled_buffer_140_out = or_8_out ? rom_1_data[5] : 1'bz;  // Controlled_Buffer controlled_buffer_143
  D_Flip_Flop #(.trigger("falling")) d_ff_41 (
    .D(controlled_buffer_140_out), .clk(controlled_buffer_141_out), .Q(d_ff_32_q[5]), .Qn(d_ff_41_qn));  // open: preset, reset
  assign controlled_buffer_144_out = not_14_out ? d_ff_42_qn : 1'bz;  // Controlled_Buffer controlled_buffer_144
  assign controlled_buffer_144_out = or_8_out ? rom_1_data[6] : 1'bz;  // Controlled_Buffer controlled_buffer_145
  D_Flip_Flop #(.trigger("falling")) d_ff_42 (
    .D(controlled_buffer_144_out), .clk(controlled_buffer_146_out), .Q(d_ff_32_q[6]), .Qn(d_ff_42_qn));  // open: preset, reset
  assign controlled_buffer_146_out = not_14_out ? d_ff_32_q[5] : 1'bz;  // Controlled_Buffer controlled_buffer_146
  assign controlled_buffer_146_out = or_8_out ? controlled_buffer_141_out : 1'bz;  // Controlled_Buffer controlled_buffer_147
  assign controlled_buffer_148_out = or_8_out ? rom_1_data[7] : 1'bz;  // Controlled_Buffer controlled_buffer_148
  assign controlled_buffer_148_out = not_14_out ? d_ff_43_qn : 1'bz;  // Controlled_Buffer controlled_buffer_149
  assign controlled_buffer_150_out = not_14_out ? d_ff_32_q[6] : 1'bz;  // Controlled_Buffer controlled_buffer_150
  assign controlled_buffer_150_out = or_8_out ? controlled_buffer_146_out : 1'bz;  // Controlled_Buffer controlled_buffer_151
  D_Flip_Flop #(.trigger("falling")) d_ff_43 (
    .D(controlled_buffer_148_out), .clk(controlled_buffer_150_out), .Q(d_ff_32_q[7]), .Qn(d_ff_43_qn));  // open: preset, reset
  or or_10 (or_10_out, decoder_6_out10, decoder_6_out9);
  assign controlled_buffer_152_out = or_10_out ? d_ff_28_q : 1'bz;  // Controlled_Buffer controlled_buffer_152
  or or_11 (or_11_out, decoder_6_out3, decoder_6_out4, decoder_6_out5);
  Pull_Resistor pull_resistor_84 (.node(controlled_buffer_152_out));
  not not_15 (not_15_out, clock_1_out);
  or or_12 (or_12_out, decoder_6_out3, decoder_6_out4);
  not not_16 (not_16_out, clock_1_out);
  and and_17 (and_17_out, not_16_out, decoder_5_out2);
  assign controlled_buffer_153_out = decoder_6_out9 ? controlled_buffer_152_out : 1'bz;  // Controlled_Buffer controlled_buffer_153
  assign controlled_buffer_154_out = decoder_6_out9 ? decoder_5_out2 : 1'bz;  // Controlled_Buffer controlled_buffer_154
  not not_17 (not_17_out, clock_1_out);
  not not_18 (not_18_out, clock_1_out);
  not not_19 (not_19_out, clock_1_out);
  assign controlled_buffer_155_out = decoder_6_out5 ? controlled_buffer_32_out : 1'bz;  // Controlled_Buffer controlled_buffer_155
  assign controlled_buffer_155_out = or_12_out ? controlled_buffer_32_out : 1'bz;  // Controlled_Buffer controlled_buffer_156
  assign controlled_buffer_157_out = or_12_out ? controlled_buffer_33_out : 1'bz;  // Controlled_Buffer controlled_buffer_157
  not not_20 (not_20_out, controlled_buffer_33_out);
  assign controlled_buffer_158_out = decoder_6_out5 ? controlled_buffer_30_out : 1'bz;  // Controlled_Buffer controlled_buffer_158
  assign controlled_buffer_158_out = or_12_out ? controlled_buffer_30_out : 1'bz;  // Controlled_Buffer controlled_buffer_159
  assign controlled_buffer_160_out = or_12_out ? controlled_buffer_31_out : 1'bz;  // Controlled_Buffer controlled_buffer_160
  not not_21 (not_21_out, controlled_buffer_31_out);
  assign controlled_buffer_161_out = decoder_6_out5 ? controlled_buffer_28_out : 1'bz;  // Controlled_Buffer controlled_buffer_161
  assign controlled_buffer_161_out = or_12_out ? controlled_buffer_28_out : 1'bz;  // Controlled_Buffer controlled_buffer_162
  assign controlled_buffer_163_out = or_12_out ? controlled_buffer_29_out : 1'bz;  // Controlled_Buffer controlled_buffer_163
  not not_22 (not_22_out, controlled_buffer_29_out);
  assign controlled_buffer_164_out = decoder_6_out5 ? controlled_buffer_26_out : 1'bz;  // Controlled_Buffer controlled_buffer_164
  assign controlled_buffer_164_out = or_12_out ? controlled_buffer_26_out : 1'bz;  // Controlled_Buffer controlled_buffer_165
  assign controlled_buffer_166_out = or_12_out ? controlled_buffer_27_out : 1'bz;  // Controlled_Buffer controlled_buffer_166
  not not_23 (not_23_out, controlled_buffer_27_out);
  and and_18 (and_18_out, d_ff_23_q, decoder_5_out3);
  D_Flip_Flop #(.trigger("falling")) d_ff_44 (
    .D(decoder_6_out9), .clk(and_17_out), .Q(d_ff_44_q), .reset(and_19_out));  // open: Qn, preset
  Pull_Resistor pull_resistor_85 (.node(controlled_buffer_153_out));
  and and_19 (and_19_out, decoder_5_out0, d_ff_23_q);
  Pull_Resistor pull_resistor_86 (.node(controlled_buffer_154_out));
  and and_20 (and_20_out, not_17_out, decoder_6_out9, decoder_5_out2);
  D_Flip_Flop #(.trigger("falling")) d_ff_45 (
    .D(decoder_6_out10), .clk(and_21_out), .Q(d_ff_45_q), .reset(and_22_out));  // open: Qn, preset
  and and_21 (and_21_out, not_18_out, decoder_5_out2);
  and and_22 (and_22_out, decoder_5_out0, d_ff_23_q);
  and and_23 (and_23_out, not_19_out, decoder_6_out10, decoder_5_out2);
  Pull_Resistor pull_resistor_87 (.node(controlled_buffer_155_out));
  Pull_Resistor pull_resistor_88 (.node(controlled_buffer_157_out));
  assign controlled_buffer_157_out = decoder_6_out5 ? not_20_out : 1'bz;  // Controlled_Buffer controlled_buffer_167
  Pull_Resistor pull_resistor_89 (.node(pull_resistor_89_node));
  assign pull_resistor_89_node = decoder_6_out5 ? 1'b1 : 1'bz;  // Controlled_Buffer controlled_buffer_168
  Pull_Resistor pull_resistor_90 (.node(controlled_buffer_158_out));
  Pull_Resistor pull_resistor_91 (.node(controlled_buffer_160_out));
  assign controlled_buffer_160_out = decoder_6_out5 ? not_21_out : 1'bz;  // Controlled_Buffer controlled_buffer_169
  Pull_Resistor pull_resistor_92 (.node(controlled_buffer_161_out));
  Pull_Resistor pull_resistor_93 (.node(controlled_buffer_163_out));
  assign controlled_buffer_163_out = decoder_6_out5 ? not_22_out : 1'bz;  // Controlled_Buffer controlled_buffer_170
  Pull_Resistor pull_resistor_94 (.node(controlled_buffer_164_out));
  Pull_Resistor pull_resistor_95 (.node(controlled_buffer_166_out));
  assign controlled_buffer_166_out = decoder_6_out5 ? not_23_out : 1'bz;  // Controlled_Buffer controlled_buffer_171
  and and_24 (and_24_out, decoder_6_out9, not_24_out);
  not not_24 (not_24_out, d_ff_44_q);
  not not_25 (not_25_out, controlled_buffer_153_out);
  and and_25 (and_25_out, d_ff_23_q, controlled_buffer_154_out);
  and and_26 (and_26_out, decoder_6_out9, decoder_5_out3);
  not not_26 (not_26_out, d_ff_45_q);
  and and_27 (and_27_out, d_ff_23_q, decoder_5_out2);
  xor xor_1 (xor_1_out, controlled_buffer_155_out, controlled_buffer_157_out);
  xor xor_2 (xor_2_out, controlled_buffer_158_out, controlled_buffer_160_out);
  xor xor_3 (xor_3_out, controlled_buffer_161_out, controlled_buffer_163_out);
  xor xor_4 (xor_4_out, controlled_buffer_164_out, controlled_buffer_166_out);
  Pull_Resistor pull_resistor_96 (.node(pull_resistor_96_node));
  not not_27 (not_27_out, and_25_out);
  assign pull_resistor_96_node = controlled_buffer_153_out ? not_27_out : 1'bz;  // Controlled_Buffer controlled_buffer_172
  and and_28 (and_28_out, decoder_6_out10, not_26_out);
  not not_28 (not_28_out, and_28_out);
  assign controlled_buffer_173_out = not_28_out ? and_27_out : 1'bz;  // Controlled_Buffer controlled_buffer_173
  assign controlled_buffer_173_out = and_28_out ? and_23_out : 1'bz;  // Controlled_Buffer controlled_buffer_174
  and and_29 (and_29_out, decoder_6_out10, decoder_5_out3);
  xor xor_5 (xor_5_out, xor_1_out, pull_resistor_89_node);
  and and_30 (and_30_out, pull_resistor_89_node, xor_1_out);
  and and_31 (and_31_out, controlled_buffer_157_out, controlled_buffer_155_out);
  xor xor_6 (xor_6_out, xor_2_out, or_13_out);
  and and_32 (and_32_out, or_13_out, xor_2_out);
  and and_33 (and_33_out, controlled_buffer_160_out, controlled_buffer_158_out);
  xor xor_7 (xor_7_out, xor_3_out, or_14_out);
  and and_34 (and_34_out, or_14_out, xor_3_out);
  and and_35 (and_35_out, controlled_buffer_163_out, controlled_buffer_161_out);
  xor xor_8 (xor_8_out, xor_4_out, or_15_out);
  and and_36 (and_36_out, or_15_out, xor_4_out);
  and and_37 (and_37_out, controlled_buffer_166_out, controlled_buffer_164_out);
  Pull_Resistor pull_resistor_97 (.node(pull_resistor_97_node));
  assign pull_resistor_97_node = decoder_6_out6 ? controlled_buffer_26_out : 1'bz;  // Controlled_Buffer controlled_buffer_175
  Pull_Resistor pull_resistor_98 (.node(pull_resistor_98_node));
  assign pull_resistor_98_node = decoder_6_out6 ? controlled_buffer_27_out : 1'bz;  // Controlled_Buffer controlled_buffer_176
  Pull_Resistor pull_resistor_99 (.node(pull_resistor_99_node));
  assign pull_resistor_99_node = decoder_6_out6 ? controlled_buffer_28_out : 1'bz;  // Controlled_Buffer controlled_buffer_177
  Pull_Resistor pull_resistor_100 (.node(pull_resistor_100_node));
  assign pull_resistor_100_node = decoder_6_out6 ? controlled_buffer_29_out : 1'bz;  // Controlled_Buffer controlled_buffer_178
  Pull_Resistor pull_resistor_101 (.node(pull_resistor_101_node));
  assign pull_resistor_101_node = decoder_6_out6 ? controlled_buffer_30_out : 1'bz;  // Controlled_Buffer controlled_buffer_179
  Pull_Resistor pull_resistor_102 (.node(pull_resistor_102_node));
  assign pull_resistor_102_node = decoder_6_out6 ? controlled_buffer_31_out : 1'bz;  // Controlled_Buffer controlled_buffer_180
  Pull_Resistor pull_resistor_103 (.node(pull_resistor_103_node));
  assign pull_resistor_103_node = decoder_6_out6 ? controlled_buffer_32_out : 1'bz;  // Controlled_Buffer controlled_buffer_181
  Pull_Resistor pull_resistor_104 (.node(pull_resistor_104_node));
  assign pull_resistor_104_node = decoder_6_out6 ? controlled_buffer_33_out : 1'bz;  // Controlled_Buffer controlled_buffer_182
  Pull_Resistor pull_resistor_105 (.node(pull_resistor_105_node));
  assign pull_resistor_105_node = decoder_6_out7 ? controlled_buffer_26_out : 1'bz;  // Controlled_Buffer controlled_buffer_183
  Pull_Resistor pull_resistor_106 (.node(pull_resistor_106_node));
  assign pull_resistor_106_node = decoder_6_out7 ? controlled_buffer_27_out : 1'bz;  // Controlled_Buffer controlled_buffer_184
  Pull_Resistor pull_resistor_107 (.node(pull_resistor_107_node));
  assign pull_resistor_107_node = decoder_6_out7 ? controlled_buffer_28_out : 1'bz;  // Controlled_Buffer controlled_buffer_185
  Pull_Resistor pull_resistor_108 (.node(pull_resistor_108_node));
  assign pull_resistor_108_node = decoder_6_out7 ? controlled_buffer_29_out : 1'bz;  // Controlled_Buffer controlled_buffer_186
  Pull_Resistor pull_resistor_109 (.node(pull_resistor_109_node));
  assign pull_resistor_109_node = decoder_6_out7 ? controlled_buffer_30_out : 1'bz;  // Controlled_Buffer controlled_buffer_187
  Pull_Resistor pull_resistor_110 (.node(pull_resistor_110_node));
  assign pull_resistor_110_node = decoder_6_out7 ? controlled_buffer_31_out : 1'bz;  // Controlled_Buffer controlled_buffer_188
  Pull_Resistor pull_resistor_111 (.node(pull_resistor_111_node));
  assign pull_resistor_111_node = decoder_6_out7 ? controlled_buffer_32_out : 1'bz;  // Controlled_Buffer controlled_buffer_189
  Pull_Resistor pull_resistor_112 (.node(pull_resistor_112_node));
  assign pull_resistor_112_node = decoder_6_out7 ? controlled_buffer_33_out : 1'bz;  // Controlled_Buffer controlled_buffer_190
  Pull_Resistor pull_resistor_113 (.node(pull_resistor_113_node));
  assign pull_resistor_113_node = decoder_6_out8 ? controlled_buffer_26_out : 1'bz;  // Controlled_Buffer controlled_buffer_191
  Pull_Resistor pull_resistor_114 (.node(pull_resistor_114_node));
  assign pull_resistor_114_node = decoder_6_out8 ? controlled_buffer_27_out : 1'bz;  // Controlled_Buffer controlled_buffer_192
  Pull_Resistor pull_resistor_115 (.node(pull_resistor_115_node));
  assign pull_resistor_115_node = decoder_6_out8 ? controlled_buffer_28_out : 1'bz;  // Controlled_Buffer controlled_buffer_193
  Pull_Resistor pull_resistor_116 (.node(pull_resistor_116_node));
  assign pull_resistor_116_node = decoder_6_out8 ? controlled_buffer_29_out : 1'bz;  // Controlled_Buffer controlled_buffer_194
  Pull_Resistor pull_resistor_117 (.node(pull_resistor_117_node));
  assign pull_resistor_117_node = decoder_6_out8 ? controlled_buffer_30_out : 1'bz;  // Controlled_Buffer controlled_buffer_195
  Pull_Resistor pull_resistor_118 (.node(pull_resistor_118_node));
  assign pull_resistor_118_node = decoder_6_out8 ? controlled_buffer_31_out : 1'bz;  // Controlled_Buffer controlled_buffer_196
  Pull_Resistor pull_resistor_119 (.node(pull_resistor_119_node));
  assign pull_resistor_119_node = decoder_6_out8 ? controlled_buffer_32_out : 1'bz;  // Controlled_Buffer controlled_buffer_197
  Pull_Resistor pull_resistor_120 (.node(pull_resistor_120_node));
  assign pull_resistor_120_node = decoder_6_out8 ? controlled_buffer_33_out : 1'bz;  // Controlled_Buffer controlled_buffer_198
  not not_29 (not_29_out, and_24_out);
  assign controlled_buffer_199_out = and_24_out ? controlled_buffer_32_out : 1'bz;  // Controlled_Buffer controlled_buffer_199
  D_Flip_Flop d_ff_46 (
    .D(controlled_buffer_199_out), .clk(controlled_buffer_202_out), .Q(d_ff_46_q), .Qn(d_ff_46_qn));  // open: preset, reset
  Pull_Resistor pull_resistor_121 (.node(controlled_buffer_199_out));
  assign controlled_buffer_199_out = not_29_out ? d_ff_46_qn : 1'bz;  // Controlled_Buffer controlled_buffer_200
  assign pull_resistor_96_node = not_25_out ? and_25_out : 1'bz;  // Controlled_Buffer controlled_buffer_201
  assign controlled_buffer_202_out = not_30_out ? pull_resistor_96_node : 1'bz;  // Controlled_Buffer controlled_buffer_202
  assign controlled_buffer_202_out = and_24_out ? and_20_out : 1'bz;  // Controlled_Buffer controlled_buffer_203
  not not_30 (not_30_out, and_24_out);
  Pull_Resistor pull_resistor_122 (.node(pull_resistor_122_node));
  assign pull_resistor_122_node = not_28_out ? controlled_buffer_152_out : 1'bz;  // Controlled_Buffer controlled_buffer_204
  or or_13 (or_13_out, and_30_out, and_31_out);
  or or_14 (or_14_out, and_32_out, and_33_out);
  or or_15 (or_15_out, and_34_out, and_35_out);
  D_Flip_Flop d_ff_47 (.D(or_16_out), .clk(pull_resistor_123_node), .Q(d_ff_47_q));  // open: Qn, preset, reset
  or or_16 (or_16_out, and_36_out, and_37_out);
  Pull_Resistor pull_resistor_123 (.node(pull_resistor_123_node));
  assign pull_resistor_123_node = or_12_out ? and_18_out : 1'bz;  // Controlled_Buffer controlled_buffer_205
  and and_38 (and_38_out, pull_resistor_97_node, pull_resistor_98_node);
  and and_39 (and_39_out, pull_resistor_99_node, pull_resistor_100_node);
  and and_40 (and_40_out, pull_resistor_101_node, pull_resistor_102_node);
  and and_41 (and_41_out, pull_resistor_103_node, pull_resistor_104_node);
  or or_17 (or_17_out, pull_resistor_105_node, pull_resistor_106_node);
  or or_18 (or_18_out, pull_resistor_107_node, pull_resistor_108_node);
  or or_19 (or_19_out, pull_resistor_109_node, pull_resistor_110_node);
  or or_20 (or_20_out, pull_resistor_111_node, pull_resistor_112_node);
  xor xor_9 (xor_9_out, pull_resistor_113_node, pull_resistor_114_node);
  xor xor_10 (xor_10_out, pull_resistor_115_node, pull_resistor_116_node);
  xor xor_11 (xor_11_out, pull_resistor_117_node, pull_resistor_118_node);
  xor xor_12 (xor_12_out, pull_resistor_119_node, pull_resistor_120_node);
  assign controlled_buffer_87_out = and_26_out ? d_ff_46_q : 1'bz;  // Controlled_Buffer controlled_buffer_206
  not not_31 (not_31_out, pull_resistor_122_node);
  assign controlled_buffer_207_out = not_28_out ? not_31_out : 1'bz;  // Controlled_Buffer controlled_buffer_207
  assign controlled_buffer_208_out = pull_resistor_122_node ? 1'b0 : 1'bz;  // Controlled_Buffer controlled_buffer_208
  assign pull_resistor_89_node = decoder_6_out4 ? d_ff_47_q : 1'bz;  // Controlled_Buffer controlled_buffer_209
  assign controlled_buffer_90_out = decoder_6_out6 ? and_38_out : 1'bz;  // Controlled_Buffer controlled_buffer_210
  assign controlled_buffer_89_out = decoder_6_out6 ? and_39_out : 1'bz;  // Controlled_Buffer controlled_buffer_211
  assign controlled_buffer_88_out = decoder_6_out6 ? and_40_out : 1'bz;  // Controlled_Buffer controlled_buffer_212
  assign controlled_buffer_87_out = decoder_6_out6 ? and_41_out : 1'bz;  // Controlled_Buffer controlled_buffer_213
  assign controlled_buffer_90_out = decoder_6_out7 ? or_17_out : 1'bz;  // Controlled_Buffer controlled_buffer_214
  assign controlled_buffer_89_out = decoder_6_out7 ? or_18_out : 1'bz;  // Controlled_Buffer controlled_buffer_215
  assign controlled_buffer_88_out = decoder_6_out7 ? or_19_out : 1'bz;  // Controlled_Buffer controlled_buffer_216
  assign controlled_buffer_87_out = decoder_6_out7 ? or_20_out : 1'bz;  // Controlled_Buffer controlled_buffer_217
  assign controlled_buffer_90_out = decoder_6_out8 ? xor_9_out : 1'bz;  // Controlled_Buffer controlled_buffer_218
  assign controlled_buffer_89_out = decoder_6_out8 ? xor_10_out : 1'bz;  // Controlled_Buffer controlled_buffer_219
  assign controlled_buffer_88_out = decoder_6_out8 ? xor_11_out : 1'bz;  // Controlled_Buffer controlled_buffer_220
  assign controlled_buffer_87_out = decoder_6_out8 ? xor_12_out : 1'bz;  // Controlled_Buffer controlled_buffer_221
  Pull_Resistor pull_resistor_124 (.node(pull_resistor_124_node));
  not not_32 (not_32_out, d_ff_46_q);
  assign pull_resistor_124_node = controlled_buffer_153_out ? not_32_out : 1'bz;  // Controlled_Buffer controlled_buffer_222
  assign controlled_buffer_208_out = and_28_out ? controlled_buffer_32_out : 1'bz;  // Controlled_Buffer controlled_buffer_223
  D_Flip_Flop d_ff_48 (
    .D(controlled_buffer_208_out), .clk(controlled_buffer_173_out), .Q(d_ff_48_q));  // open: Qn, preset, reset
  Pull_Resistor pull_resistor_125 (.node(controlled_buffer_208_out));
  assign controlled_buffer_87_out = or_11_out ? xor_5_out : 1'bz;  // Controlled_Buffer controlled_buffer_224
  assign controlled_buffer_88_out = or_11_out ? xor_6_out : 1'bz;  // Controlled_Buffer controlled_buffer_225
  assign controlled_buffer_89_out = or_11_out ? xor_7_out : 1'bz;  // Controlled_Buffer controlled_buffer_226
  assign controlled_buffer_90_out = or_11_out ? xor_8_out : 1'bz;  // Controlled_Buffer controlled_buffer_227
  assign controlled_buffer_228_out = and_24_out ? controlled_buffer_30_out : 1'bz;  // Controlled_Buffer controlled_buffer_228
  D_Flip_Flop d_ff_49 (
    .D(controlled_buffer_228_out), .clk(controlled_buffer_231_out), .Q(d_ff_49_q), .Qn(d_ff_49_qn));  // open: preset, reset
  assign controlled_buffer_228_out = not_29_out ? d_ff_49_qn : 1'bz;  // Controlled_Buffer controlled_buffer_229
  assign pull_resistor_124_node = not_25_out ? d_ff_46_q : 1'bz;  // Controlled_Buffer controlled_buffer_230
  assign controlled_buffer_231_out = not_30_out ? pull_resistor_124_node : 1'bz;  // Controlled_Buffer controlled_buffer_231
  assign controlled_buffer_231_out = and_24_out ? and_20_out : 1'bz;  // Controlled_Buffer controlled_buffer_232
  assign controlled_buffer_233_out = and_28_out ? controlled_buffer_30_out : 1'bz;  // Controlled_Buffer controlled_buffer_233
  assign controlled_buffer_208_out = controlled_buffer_207_out ? d_ff_50_q : 1'bz;  // Controlled_Buffer controlled_buffer_234
  D_Flip_Flop d_ff_50 (
    .D(controlled_buffer_233_out), .clk(controlled_buffer_173_out), .Q(d_ff_50_q));  // open: Qn, preset, reset
  Pull_Resistor pull_resistor_126 (.node(controlled_buffer_233_out));
  assign controlled_buffer_233_out = pull_resistor_122_node ? d_ff_48_q : 1'bz;  // Controlled_Buffer controlled_buffer_235
  assign controlled_buffer_87_out = and_29_out ? d_ff_48_q : 1'bz;  // Controlled_Buffer controlled_buffer_236
  Pull_Resistor pull_resistor_127 (.node(or_11_out));
  assign controlled_buffer_88_out = and_26_out ? d_ff_49_q : 1'bz;  // Controlled_Buffer controlled_buffer_237
  assign controlled_buffer_238_out = pull_resistor_122_node ? d_ff_50_q : 1'bz;  // Controlled_Buffer controlled_buffer_238
  assign controlled_buffer_88_out = and_29_out ? d_ff_50_q : 1'bz;  // Controlled_Buffer controlled_buffer_239
  Pull_Resistor pull_resistor_128 (.node(pull_resistor_128_node));
  not not_33 (not_33_out, d_ff_49_q);
  assign pull_resistor_128_node = controlled_buffer_153_out ? not_33_out : 1'bz;  // Controlled_Buffer controlled_buffer_240
  assign controlled_buffer_238_out = and_28_out ? controlled_buffer_28_out : 1'bz;  // Controlled_Buffer controlled_buffer_241
  assign controlled_buffer_233_out = controlled_buffer_207_out ? d_ff_51_q : 1'bz;  // Controlled_Buffer controlled_buffer_242
  D_Flip_Flop d_ff_51 (
    .D(controlled_buffer_238_out), .clk(controlled_buffer_173_out), .Q(d_ff_51_q));  // open: Qn, preset, reset
  Pull_Resistor pull_resistor_129 (.node(controlled_buffer_238_out));
  assign controlled_buffer_243_out = and_24_out ? controlled_buffer_28_out : 1'bz;  // Controlled_Buffer controlled_buffer_243
  D_Flip_Flop d_ff_52 (
    .D(controlled_buffer_243_out), .clk(controlled_buffer_246_out), .Q(d_ff_52_q), .Qn(d_ff_52_qn));  // open: preset, reset
  assign controlled_buffer_243_out = not_29_out ? d_ff_52_qn : 1'bz;  // Controlled_Buffer controlled_buffer_244
  assign pull_resistor_128_node = not_25_out ? d_ff_49_q : 1'bz;  // Controlled_Buffer controlled_buffer_245
  assign controlled_buffer_246_out = not_30_out ? pull_resistor_128_node : 1'bz;  // Controlled_Buffer controlled_buffer_246
  assign controlled_buffer_246_out = and_24_out ? and_20_out : 1'bz;  // Controlled_Buffer controlled_buffer_247
  assign controlled_buffer_248_out = and_28_out ? controlled_buffer_26_out : 1'bz;  // Controlled_Buffer controlled_buffer_248
  assign controlled_buffer_238_out = controlled_buffer_207_out ? d_ff_53_q : 1'bz;  // Controlled_Buffer controlled_buffer_249
  D_Flip_Flop d_ff_53 (
    .D(controlled_buffer_248_out), .clk(controlled_buffer_173_out), .Q(d_ff_53_q));  // open: Qn, preset, reset
  Pull_Resistor pull_resistor_130 (.node(controlled_buffer_248_out));
  assign controlled_buffer_248_out = pull_resistor_122_node ? d_ff_51_q : 1'bz;  // Controlled_Buffer controlled_buffer_250
  Pull_Resistor pull_resistor_131 (.node(controlled_buffer_173_out));
  assign controlled_buffer_89_out = and_29_out ? d_ff_51_q : 1'bz;  // Controlled_Buffer controlled_buffer_251
  assign controlled_buffer_89_out = and_26_out ? d_ff_52_q : 1'bz;  // Controlled_Buffer controlled_buffer_252
  assign controlled_buffer_248_out = controlled_buffer_207_out ? 1'b0 : 1'bz;  // Controlled_Buffer controlled_buffer_253
  assign controlled_buffer_90_out = and_29_out ? d_ff_53_q : 1'bz;  // Controlled_Buffer controlled_buffer_254
  Pull_Resistor pull_resistor_132 (.node(pull_resistor_132_node));
  not not_34 (not_34_out, d_ff_52_q);
  assign pull_resistor_132_node = controlled_buffer_153_out ? not_34_out : 1'bz;  // Controlled_Buffer controlled_buffer_255
  Pull_Resistor pull_resistor_133 (.node(controlled_buffer_207_out));
  assign controlled_buffer_256_out = and_24_out ? controlled_buffer_26_out : 1'bz;  // Controlled_Buffer controlled_buffer_256
  D_Flip_Flop d_ff_54 (
    .D(controlled_buffer_256_out), .clk(controlled_buffer_259_out), .Q(d_ff_54_q), .Qn(d_ff_54_qn));  // open: preset, reset
  assign controlled_buffer_256_out = not_29_out ? d_ff_54_qn : 1'bz;  // Controlled_Buffer controlled_buffer_257
  assign pull_resistor_132_node = not_25_out ? d_ff_52_q : 1'bz;  // Controlled_Buffer controlled_buffer_258
  assign controlled_buffer_259_out = not_30_out ? pull_resistor_132_node : 1'bz;  // Controlled_Buffer controlled_buffer_259
  assign controlled_buffer_259_out = and_24_out ? and_20_out : 1'bz;  // Controlled_Buffer controlled_buffer_260
  assign controlled_buffer_90_out = and_26_out ? d_ff_54_q : 1'bz;  // Controlled_Buffer controlled_buffer_261
  Pull_Resistor pull_resistor_134 (.node(controlled_buffer_90_out));
  Pull_Resistor pull_resistor_135 (.node(controlled_buffer_89_out));
  Pull_Resistor pull_resistor_136 (.node(controlled_buffer_88_out));
  Pull_Resistor pull_resistor_137 (.node(controlled_buffer_87_out));

  // Notes on the sheet:
  //   contents of rom_1 (hex, n*v repeats v):
  //   b0 0 b8 0 b4 f bc f e4 13 33 f0 f d0 10 99 94 d0 8 20 10 22 11 d0 17
endmodule
