// Logisim project CPUwithMicrocircuits.circ as structural Verilog: 1 circuit, main circuit main
module main (
);

  wire and_1_out, and_2_out, clock_1_out, n7400_1_pin8, n7400_1_pin9, n7400_1_pin10, n7400_1_pin11,
       n7400_1_pin12, n7404_1_pin2, n7404_1_pin4, n7404_1_pin8, n7404_1_pin10, n7404_1_pin12, n7404_2_pin1,
       n7404_2_pin4, n7404_3_pin10, n7404_3_pin11, n7404_3_pin12, n7404_4_pin2, n7404_4_pin4, n7404_4_pin5,
       n7404_4_pin6, n7404_4_pin8, n7404_4_pin10, n7404_4_pin12, n7404_5_pin4, n7404_5_pin6, n7404_5_pin8,
       n7404_5_pin12, n7408_1_pin1, n7408_1_pin2, n7408_1_pin3, n7408_1_pin4, n7408_1_pin5, n7408_1_pin6,
       n7408_1_pin9, n7408_2_pin1, n7408_2_pin2, n7408_2_pin3, n7408_2_pin4, n7408_2_pin5, n7408_2_pin9,
       n7408_2_pin10, n7408_2_pin12, n7408_2_pin13, n7408_3_pin2, n7408_3_pin3, n7408_3_pin4, n7408_3_pin5,
       n7408_3_pin9, n7408_3_pin10, n7408_3_pin12, n7408_3_pin13, n7408_4_pin2, n7408_4_pin4, n7408_4_pin5,
       n7408_4_pin9, n7408_4_pin10, n7408_4_pin12, n7408_4_pin13, n7408_5_pin3, n7408_5_pin6, n7408_5_pin11,
       n7408_6_pin3, n7408_6_pin6, n7408_6_pin8, n7408_6_pin11, n7408_6_pin12, n7408_7_pin6, n7408_7_pin8,
       n7408_7_pin11, n7408_8_pin8, n7408_9_pin3, n7408_9_pin6, n7408_9_pin8, n7408_9_pin11, n7432_1_pin9,
       n7432_1_pin11, n7432_1_pin12, n7432_1_pin13, n7432_2_pin1, n7432_2_pin3, n7432_2_pin6, n7432_2_pin8,
       n7432_2_pin10, n7432_2_pin11, n7432_3_pin3, n7432_3_pin6, n7432_3_pin8, n7432_3_pin11, n7474_1_pin3,
       n7474_1_pin5, n7474_2_pin2, n7474_2_pin3, n7474_2_pin5, n7486_1_pin3, n7486_1_pin6, n7486_1_pin8,
       n7486_1_pin11, n74139_1_pin1, n74139_1_pin2, n74139_1_pin3, n74139_1_pin4, n74139_1_pin5,
       n74139_1_pin6, n74139_1_pin7, n74139_1_pin9, n74139_1_pin10, n74139_1_pin11, n74139_1_pin12,
       n74139_1_pin13, n74139_1_pin14, n74139_2_pin4, n74139_2_pin5, n74139_2_pin6, n74139_2_pin7,
       n74161_1_pin1, n74161_1_pin2, n74161_1_pin3, n74161_1_pin12, n74161_1_pin13, n74161_1_pin14,
       n74194_1_pin12, n74194_1_pin13, n74194_1_pin14, n74194_1_pin15, n74244_1_pin3, n74244_1_pin5,
       n74244_1_pin7, n74244_1_pin9, n74244_1_pin12, n74244_1_pin14, n74244_1_pin16, n74244_1_pin18,
       n74244_7_pin1, n74244_7_pin3, n74244_7_pin5, n74244_7_pin7, n74244_7_pin9, n74244_7_pin12,
       n74244_7_pin14, n74244_7_pin16, n74244_7_pin18, n74283_1_pin1, n74283_1_pin4, n74283_1_pin7,
       n74283_1_pin10, n74283_1_pin13, not_1_out, not_2_out, not_3_out, not_4_out, sub74hc173_1_out_13,
       sub74hc173_1_out_14, sub74hc173_1_out_15, sub74hc173_1_out_16, sub74hc173_2_out_13,
       sub74hc173_2_out_14, sub74hc173_2_out_15, sub74hc173_2_out_16, sub74hc173_3_out_13,
       sub74hc173_3_out_14, sub74hc173_3_out_15, sub74hc173_3_out_16, sub74hc173_4_out_13,
       sub74hc173_4_out_14, sub74hc173_4_out_15, sub74hc173_4_out_16, sub74hc173_6_out_13,
       sub74hc173_6_out_14, sub74hc173_6_out_15, sub74hc173_6_out_16, sub74hc191_1_out_11,
       sub74hc191_1_out_12, sub74hc191_1_out_13, sub74hc191_1_out_14;
  wire [3:0] controlled_buffer_2_out, n74244_5_pin3, n74244_5_pin18, ram_1_dout;
  wire [7:0] controlled_buffer_1_out, n74161_2_pin14, n74244_5_pin17;

  Clock clock_1 (.out(clock_1_out));
  _74139 u_74139_1 (
    .pin1(n74139_1_pin1), .pin2(n74139_1_pin2), .pin3(n74139_1_pin3), .pin4(n74139_1_pin4),
    .pin5(n74139_1_pin5), .pin6(n74139_1_pin6), .pin7(n74139_1_pin7), .pin15(n74139_1_pin1),
    .pin14(n74139_1_pin14), .pin13(n74139_1_pin13), .pin12(n74139_1_pin12), .pin11(n74139_1_pin11),
    .pin10(n74139_1_pin10), .pin9(n74139_1_pin9));
  sub74HC173 sub74hc173_1 (
    .in_1(n74244_5_pin3[3]), .in_2(n74244_5_pin3[2]), .in_3(n74244_5_pin3[1]), .in_4(n74244_5_pin3[0]),
    .in_5(n74139_1_pin4), .in_6(n7408_1_pin9), .in_7(n7408_6_pin12), .in_8(n74161_1_pin3),
    .in_9(n74161_1_pin3), .in_10(n74161_1_pin3), .in_11(n74161_1_pin1), .in_12(n74161_1_pin3),
    .out_13(sub74hc173_1_out_13), .out_14(sub74hc173_1_out_14), .out_15(sub74hc173_1_out_15),
    .out_16(sub74hc173_1_out_16));
  sub74HC173 sub74hc173_2 (
    .in_1(n74244_5_pin3[3]), .in_2(n74244_5_pin3[2]), .in_3(n74244_5_pin3[1]), .in_4(n74244_5_pin3[0]),
    .in_5(n74139_1_pin5), .in_6(n7408_1_pin9), .in_7(n7408_6_pin12), .in_8(n74161_1_pin3),
    .in_9(n74161_1_pin3), .in_10(n74161_1_pin3), .in_11(n74161_1_pin1), .in_12(n74161_1_pin3),
    .out_13(sub74hc173_2_out_13), .out_14(sub74hc173_2_out_14), .out_15(sub74hc173_2_out_15),
    .out_16(sub74hc173_2_out_16));
  sub74HC173 sub74hc173_3 (
    .in_1(n74244_5_pin3[3]), .in_2(n74244_5_pin3[2]), .in_3(n74244_5_pin3[1]), .in_4(n74244_5_pin3[0]),
    .in_5(n74139_1_pin6), .in_6(n7408_1_pin9), .in_7(n7408_6_pin12), .in_8(n74161_1_pin3),
    .in_9(n74161_1_pin3), .in_10(n74161_1_pin3), .in_11(n74161_1_pin1), .in_12(n74161_1_pin3),
    .out_13(sub74hc173_3_out_13), .out_14(sub74hc173_3_out_14), .out_15(sub74hc173_3_out_15),
    .out_16(sub74hc173_3_out_16));
  sub74HC173 sub74hc173_4 (
    .in_1(n74244_5_pin3[3]), .in_2(n74244_5_pin3[2]), .in_3(n74244_5_pin3[1]), .in_4(n74244_5_pin3[0]),
    .in_5(n74139_1_pin7), .in_6(n7408_1_pin9), .in_7(n7408_6_pin12), .in_8(n74161_1_pin3),
    .in_9(n74161_1_pin3), .in_10(n74161_1_pin3), .in_11(n74161_1_pin1), .in_12(n74161_1_pin3),
    .out_13(sub74hc173_4_out_13), .out_14(sub74hc173_4_out_14), .out_15(sub74hc173_4_out_15),
    .out_16(sub74hc173_4_out_16));
  _74161 u_74161_1 (
    .pin1(n74161_1_pin1), .pin2(n74161_1_pin2), .pin3(n74161_1_pin3), .pin4(n74161_1_pin3),
    .pin5(n74161_1_pin3), .pin6(n74161_1_pin3), .pin7(n74161_1_pin1), .pin14(n74161_1_pin14),
    .pin13(n74161_1_pin13), .pin12(n74161_1_pin12), .pin10(n74161_1_pin1), .pin9(n74161_1_pin1));  // open: pin15, pin11
  _74139 u_74139_2 (
    .pin1(n74161_1_pin3), .pin2(n74161_1_pin13), .pin3(n74161_1_pin12), .pin4(n74139_2_pin4),
    .pin5(n74139_2_pin5), .pin6(n74139_2_pin6), .pin7(n74139_2_pin7), .pin15(n74161_1_pin3),
    .pin14(n74161_1_pin3), .pin13(n74161_1_pin3));  // open: pin12, pin11, pin10, pin9
  _7404 u_7404_1 (
    .pin1(n74139_2_pin4), .pin2(n7404_1_pin2), .pin3(n74161_1_pin14), .pin4(n7404_1_pin4),
    .pin5(clock_1_out), .pin6(n74161_1_pin2), .pin13(n74139_2_pin7), .pin12(n7404_1_pin12),
    .pin11(n74139_2_pin6), .pin10(n7404_1_pin10), .pin9(n74139_2_pin5), .pin8(n7404_1_pin8));
  _74244 u_74244_1 (
    .pin1(n74139_1_pin4), .pin2(sub74hc173_1_out_16), .pin3(n74244_1_pin3), .pin4(sub74hc173_1_out_15),
    .pin5(n74244_1_pin5), .pin6(sub74hc173_1_out_14), .pin7(n74244_1_pin7), .pin8(sub74hc173_1_out_13),
    .pin9(n74244_1_pin9), .pin19(n74139_1_pin12), .pin18(n74244_1_pin18), .pin17(sub74hc173_1_out_16),
    .pin16(n74244_1_pin16), .pin15(sub74hc173_1_out_15), .pin14(n74244_1_pin14), .pin13(sub74hc173_1_out_14),
    .pin12(n74244_1_pin12), .pin11(sub74hc173_1_out_13));
  _74244 u_74244_2 (
    .pin1(n74139_1_pin5), .pin2(sub74hc173_2_out_16), .pin3(n74244_1_pin3), .pin4(sub74hc173_2_out_15),
    .pin5(n74244_1_pin5), .pin6(sub74hc173_2_out_14), .pin7(n74244_1_pin7), .pin8(sub74hc173_2_out_13),
    .pin9(n74244_1_pin9), .pin19(n74139_1_pin11), .pin18(n74244_1_pin18), .pin17(sub74hc173_2_out_16),
    .pin16(n74244_1_pin16), .pin15(sub74hc173_2_out_15), .pin14(n74244_1_pin14), .pin13(sub74hc173_2_out_14),
    .pin12(n74244_1_pin12), .pin11(sub74hc173_2_out_13));
  _74244 u_74244_3 (
    .pin1(n74139_1_pin6), .pin2(sub74hc173_3_out_16), .pin3(n74244_1_pin3), .pin4(sub74hc173_3_out_15),
    .pin5(n74244_1_pin5), .pin6(sub74hc173_3_out_14), .pin7(n74244_1_pin7), .pin8(sub74hc173_3_out_13),
    .pin9(n74244_1_pin9), .pin19(n74139_1_pin10), .pin18(n74244_1_pin18), .pin17(sub74hc173_3_out_16),
    .pin16(n74244_1_pin16), .pin15(sub74hc173_3_out_15), .pin14(n74244_1_pin14), .pin13(sub74hc173_3_out_14),
    .pin12(n74244_1_pin12), .pin11(sub74hc173_3_out_13));
  _74244 u_74244_4 (
    .pin1(n74139_1_pin7), .pin2(sub74hc173_4_out_16), .pin3(n74244_1_pin3), .pin4(sub74hc173_4_out_15),
    .pin5(n74244_1_pin5), .pin6(sub74hc173_4_out_14), .pin7(n74244_1_pin7), .pin8(sub74hc173_4_out_13),
    .pin9(n74244_1_pin9), .pin19(n74139_1_pin9), .pin18(n74244_1_pin18), .pin17(sub74hc173_4_out_16),
    .pin16(n74244_1_pin16), .pin15(sub74hc173_4_out_15), .pin14(n74244_1_pin14), .pin13(sub74hc173_4_out_14),
    .pin12(n74244_1_pin12), .pin11(sub74hc173_4_out_13));
  Pull_Resistor pull_resistor_1 (.node(n74244_1_pin18));
  Pull_Resistor pull_resistor_2 (.node(n74244_1_pin16));
  _7408 u_7408_1 (
    .pin1(n7408_1_pin1), .pin2(n7408_1_pin2), .pin3(n7408_1_pin3), .pin4(n7408_1_pin4), .pin5(n7408_1_pin5),
    .pin6(n7408_1_pin6), .pin10(n7408_1_pin6), .pin9(n7408_1_pin9), .pin8(n74139_1_pin1));  // open: pin13, pin12, pin11
  _7408 u_7408_2 (
    .pin1(n7408_2_pin1), .pin2(n7408_2_pin2), .pin3(n7408_2_pin3), .pin4(n7408_2_pin4), .pin5(n7408_2_pin5),
    .pin6(n7408_2_pin1), .pin13(n7408_2_pin13), .pin12(n7408_2_pin12), .pin11(n7408_2_pin5),
    .pin10(n7408_2_pin10), .pin9(n7408_2_pin9), .pin8(n7408_2_pin4));
  _7408 u_7408_3 (
    .pin1(n7408_2_pin3), .pin2(n7408_3_pin2), .pin3(n7408_3_pin3), .pin4(n7408_3_pin4), .pin5(n7408_3_pin5),
    .pin6(n7408_2_pin2), .pin13(n7408_3_pin13), .pin12(n7408_3_pin12), .pin11(n7408_3_pin5),
    .pin10(n7408_3_pin10), .pin9(n7408_3_pin9), .pin8(n7408_3_pin4));
  _7408 u_7408_4 (
    .pin1(n7408_3_pin3), .pin2(n7408_4_pin2), .pin3(n7408_1_pin9), .pin4(n7408_4_pin4), .pin5(n7408_4_pin5),
    .pin6(n7408_3_pin2), .pin13(n7408_4_pin13), .pin12(n7408_4_pin12), .pin11(n7408_4_pin5),
    .pin10(n7408_4_pin10), .pin9(n7408_4_pin9), .pin8(n7408_4_pin4));
  Pull_Resistor pull_resistor_3 (.node(n74244_1_pin3));
  Pull_Resistor pull_resistor_4 (.node(n74244_1_pin14));
  Pull_Resistor pull_resistor_5 (.node(n74244_1_pin12));
  Pull_Resistor pull_resistor_6 (.node(n74244_1_pin5));
  Pull_Resistor pull_resistor_7 (.node(n74244_1_pin7));
  Pull_Resistor pull_resistor_8 (.node(n74244_1_pin9));
  _7402 u_7402_1 (
    .pin13(n7408_1_pin1), .pin12(n74244_1_pin18), .pin11(n74244_1_pin16), .pin10(n7408_1_pin2),
    .pin9(n74244_1_pin14), .pin8(n74244_1_pin12));  // open: pin1, pin2, pin3, pin4, pin5, pin6
  _7408 u_7408_5 (
    .pin1(clock_1_out), .pin2(n7404_1_pin4), .pin3(n7408_5_pin3), .pin4(n7408_5_pin3), .pin5(n7404_1_pin8),
    .pin6(n7408_5_pin6), .pin13(n7404_1_pin4), .pin12(n7404_1_pin10), .pin11(n7408_5_pin11),
    .pin9(n7408_5_pin6));  // open: pin10, pin8
  _7408 u_7408_6 (
    .pin1(n7404_1_pin10), .pin2(clock_1_out), .pin3(n7408_6_pin3), .pin4(n7404_1_pin12), .pin5(n7404_1_pin4),
    .pin6(n7408_6_pin6), .pin13(n74161_1_pin2), .pin12(n7408_6_pin12), .pin11(n7408_6_pin11),
    .pin10(clock_1_out), .pin9(n7408_6_pin6), .pin8(n7408_6_pin8));
  _7408 u_7408_7 (
    .pin1(n74161_1_pin14), .pin2(n7404_1_pin12), .pin3(n7408_6_pin12), .pin4(n74161_1_pin14),
    .pin5(n7404_1_pin10), .pin6(n7408_7_pin6), .pin13(n74161_1_pin14), .pin12(n7404_1_pin2),
    .pin11(n7408_7_pin11), .pin10(n74161_1_pin14), .pin9(n7404_1_pin8), .pin8(n7408_7_pin8));
  _7400 u_7400_1 (
    .pin13(n7408_7_pin6), .pin12(n7400_1_pin12), .pin11(n7400_1_pin11), .pin10(n7400_1_pin10),
    .pin9(n7400_1_pin9), .pin8(n7400_1_pin8));  // open: pin1, pin2, pin3, pin4, pin5, pin6
  _74244 u_74244_5 (
    .pin1(n7408_1_pin5), .pin2(n74244_1_pin3), .pin3(n74244_5_pin3[0]), .pin4(n74244_1_pin5),
    .pin5(n74244_5_pin3[1]), .pin6(n74244_1_pin7), .pin7(n74244_5_pin3[2]), .pin8(n74244_1_pin9),
    .pin9(n74244_5_pin3[3]), .pin19(n7408_4_pin13), .pin18(n74244_5_pin18[0]), .pin17(n74244_5_pin17[0]),
    .pin16(n74244_5_pin18[1]), .pin15(n74244_5_pin17[1]), .pin14(n74244_5_pin18[2]),
    .pin13(n74244_5_pin17[2]), .pin12(n74244_5_pin18[3]), .pin11(n74244_5_pin17[3]));
  _7432 u_7432_1 (
    .pin13(n7432_1_pin13), .pin12(n7432_1_pin12), .pin11(n7432_1_pin11), .pin10(n7432_1_pin11),
    .pin9(n7432_1_pin9), .pin8(n7400_1_pin9));  // open: pin1, pin2, pin3, pin4, pin5, pin6
  not not_1 (not_1_out, n7404_5_pin8);
  not not_2 (not_2_out, n7408_2_pin13);
  not not_3 (not_3_out, n7404_5_pin6);
  not not_4 (not_4_out, n7404_5_pin6);
  assign controlled_buffer_1_out = not_4_out ? n74244_5_pin17 : 8'bz;  // Controlled_Buffer controlled_buffer_1
  RAM #(.dataWidth(4), .trigger("high")) ram_1 (
    .addr(controlled_buffer_1_out), .we(and_1_out), .oe(and_2_out), .din(controlled_buffer_2_out),
    .dout(ram_1_dout));
  and and_1 (and_1_out, not_1_out, not_3_out);
  and and_2 (and_2_out, not_2_out, not_3_out);
  assign controlled_buffer_2_out = and_1_out ? n74244_5_pin18 : 4'bz;  // Controlled_Buffer controlled_buffer_2
  _7474 u_7474_1 (
    .pin1(n74161_1_pin1), .pin2(n7400_1_pin12), .pin3(n7474_1_pin3), .pin4(n74161_1_pin1),
    .pin5(n7474_1_pin5), .pin6(n7400_1_pin12), .pin13(n7400_1_pin11), .pin12(n7400_1_pin9),
    .pin11(n7400_1_pin12), .pin10(n74161_1_pin1), .pin8(n7400_1_pin10));  // open: pin9
  assign n74244_5_pin18 = and_2_out ? ram_1_dout : 4'bz;  // Controlled_Buffer controlled_buffer_3
  _7404 u_7404_2 (
    .pin1(n7404_2_pin1), .pin2(n7474_1_pin3), .pin3(n7400_1_pin8), .pin4(n7404_2_pin4),
    .pin11(n7408_2_pin13), .pin10(n7432_1_pin13), .pin9(n7408_4_pin13), .pin8(n7432_1_pin9));  // open: pin5, pin6, pin13, pin12
  Pull_Resistor pull_resistor_9 (.node(n7404_2_pin1));
  sub74HC4066 sub74hc4066_1 (
    .in_1(n7408_7_pin11), .in_2(n7404_2_pin4), .in_9(n74161_1_pin1), .in_10(n74161_1_pin3),
    .out_11(n7404_2_pin1));  // open: in_3, in_4, in_5, in_6, in_7, in_8, out_12, out_13, out_14
  _7404 u_7404_3 (
    .pin13(n7408_7_pin11), .pin12(n7404_3_pin12), .pin11(n7404_3_pin11), .pin10(n7404_3_pin10));  // open: pin1, pin2, pin3, pin4, pin5, pin6, pin9, pin8
  assign n74244_5_pin3 = and_2_out ? ram_1_dout : 4'bz;  // Controlled_Buffer controlled_buffer_4
  sub74HC154 sub74hc154_1 (
    .in_1(n74161_1_pin3), .in_2(n74161_1_pin3), .in_3(sub74hc173_6_out_13), .in_4(sub74hc173_6_out_14),
    .in_5(sub74hc173_6_out_15), .in_6(sub74hc173_6_out_16), .out_8(n7408_2_pin13), .out_9(n7408_1_pin5),
    .out_10(n7408_2_pin12), .out_11(n7408_2_pin10), .out_12(n7408_2_pin9), .out_13(n7408_3_pin13),
    .out_14(n7408_3_pin12), .out_15(n7408_3_pin10), .out_16(n7408_3_pin9), .out_17(n7408_4_pin2),
    .out_18(n7408_4_pin13), .out_19(n7408_4_pin12), .out_20(n7408_4_pin10), .out_21(n7408_1_pin4),
    .out_22(n7408_4_pin9));  // open: out_7
  ROM rom_1 (.addr(n74161_2_pin14), .data(n74244_5_pin17));
  _74161 u_74161_2 (
    .pin1(n74161_1_pin1), .pin2(n7404_3_pin12), .pin3(n74244_5_pin17[0]), .pin4(n74244_5_pin17[1]),
    .pin5(n74244_5_pin17[2]), .pin6(n74244_5_pin17[3]), .pin7(n74161_1_pin1), .pin15(n7404_3_pin11),
    .pin14(n74161_2_pin14[0]), .pin13(n74161_2_pin14[1]), .pin12(n74161_2_pin14[2]),
    .pin11(n74161_2_pin14[3]), .pin10(n74161_1_pin1), .pin9(n74161_1_pin1));
  sub74HC173 sub74hc173_5 (
    .in_1(n74244_5_pin17[0]), .in_2(n74244_5_pin17[1]), .in_3(n74244_5_pin17[2]), .in_4(n74244_5_pin17[3]),
    .in_5(n7404_2_pin4), .in_6(n7404_2_pin4), .in_7(n7408_7_pin8), .in_8(n74161_1_pin3),
    .in_9(n74161_1_pin3), .in_10(n74161_1_pin3), .in_11(n74161_1_pin1), .in_12(n74161_1_pin3),
    .out_13(n74139_1_pin14), .out_14(n74139_1_pin13), .out_15(n74139_1_pin2), .out_16(n74139_1_pin3));
  _74244 u_74244_6 (
    .pin1(n7408_4_pin12), .pin2(n74244_1_pin3), .pin4(n74244_1_pin5), .pin6(n74244_1_pin7),
    .pin8(n74244_1_pin9), .pin19(n74161_1_pin3), .pin18(n74244_5_pin3[0]), .pin17(n74161_1_pin3),
    .pin16(n74244_5_pin3[1]), .pin15(n74161_1_pin3), .pin14(n74244_5_pin3[2]), .pin13(n74161_1_pin3),
    .pin12(n74244_5_pin3[3]), .pin11(n74161_1_pin3));  // open: pin3, pin5, pin7, pin9
  _74161 u_74161_3 (
    .pin1(n74161_1_pin1), .pin2(n7404_3_pin10), .pin3(n74244_5_pin17[4]), .pin4(n74244_5_pin17[5]),
    .pin5(n74244_5_pin17[6]), .pin6(n74244_5_pin17[7]), .pin7(n74161_1_pin1), .pin14(n74161_2_pin14[4]),
    .pin13(n74161_2_pin14[5]), .pin12(n74161_2_pin14[6]), .pin11(n74161_2_pin14[7]), .pin10(n74161_1_pin1),
    .pin9(n74161_1_pin1));  // open: pin15
  sub74HC173 sub74hc173_6 (
    .in_1(n74244_5_pin17[4]), .in_2(n74244_5_pin17[5]), .in_3(n74244_5_pin17[6]), .in_4(n74244_5_pin17[7]),
    .in_5(n7404_2_pin4), .in_6(n7404_2_pin4), .in_7(n7408_7_pin8), .in_8(n74161_1_pin3),
    .in_9(n74161_1_pin3), .in_10(n74161_1_pin3), .in_11(n74161_1_pin1), .in_12(n74161_1_pin3),
    .out_13(sub74hc173_6_out_13), .out_14(sub74hc173_6_out_14), .out_15(sub74hc173_6_out_15),
    .out_16(sub74hc173_6_out_16));
  _7404 u_7404_4 (
    .pin1(n74244_1_pin9), .pin2(n7404_4_pin2), .pin3(n7408_2_pin10), .pin4(n7404_4_pin4),
    .pin5(n7404_4_pin5), .pin6(n7404_4_pin6), .pin13(n74244_1_pin3), .pin12(n7404_4_pin12),
    .pin11(n74244_1_pin5), .pin10(n7404_4_pin10), .pin9(n74244_1_pin7), .pin8(n7404_4_pin8));
  _7432 u_7432_2 (
    .pin1(n7432_2_pin1), .pin2(n7432_1_pin13), .pin3(n7432_2_pin3), .pin4(n7408_6_pin8),
    .pin5(n7408_6_pin12), .pin6(n7432_2_pin6), .pin13(n74139_1_pin14), .pin12(n7408_5_pin11),
    .pin11(n7432_2_pin11), .pin10(n7432_2_pin10), .pin9(n7408_5_pin11), .pin8(n7432_2_pin8));
  _74244 u_74244_7 (
    .pin1(n74244_7_pin1), .pin2(n74244_1_pin18), .pin3(n74244_7_pin3), .pin4(n74244_1_pin16),
    .pin5(n74244_7_pin5), .pin6(n74244_1_pin14), .pin7(n74244_7_pin7), .pin8(n74244_1_pin12),
    .pin9(n74244_7_pin9), .pin19(n74244_7_pin1), .pin18(n74244_7_pin18), .pin17(n74244_1_pin3),
    .pin16(n74244_7_pin16), .pin15(n74244_1_pin5), .pin14(n74244_7_pin14), .pin13(n74244_1_pin7),
    .pin12(n74244_7_pin12), .pin11(n74244_1_pin9));
  _7408 u_7408_8 (
    .pin1(n7408_2_pin9), .pin2(n74244_7_pin1), .pin3(n7404_4_pin5), .pin4(n7408_2_pin10),
    .pin5(n7408_2_pin12), .pin6(n74244_7_pin1), .pin13(n7432_1_pin12), .pin12(n7474_1_pin5),
    .pin11(n7432_2_pin1), .pin10(n7432_2_pin6), .pin9(n7432_2_pin3), .pin8(n7408_8_pin8));
  Pull_Resistor pull_resistor_10 (.node(n74244_7_pin9));
  Pull_Resistor pull_resistor_11 (.node(n74244_7_pin7));
  _7404 u_7404_5 (
    .pin1(n74139_1_pin14), .pin2(n7432_2_pin10), .pin3(n7408_5_pin6), .pin4(n7404_5_pin4),
    .pin5(n7408_8_pin8), .pin6(n7404_5_pin6), .pin13(n7408_2_pin9), .pin12(n7404_5_pin12),
    .pin11(n7408_1_pin5), .pin10(n7432_1_pin12), .pin9(n7432_2_pin1), .pin8(n7404_5_pin8));
  Pull_Resistor pull_resistor_12 (.node(n74244_7_pin12));
  Pull_Resistor pull_resistor_13 (.node(n74244_7_pin14));
  _74244 u_74244_8 (
    .pin1(n7408_2_pin9), .pin2(n74244_1_pin18), .pin3(n74244_7_pin3), .pin4(n74244_1_pin16),
    .pin5(n74244_7_pin5), .pin6(n74244_1_pin14), .pin7(n74244_7_pin7), .pin8(n74244_1_pin12),
    .pin9(n74244_7_pin9), .pin19(n7408_2_pin9), .pin18(n74244_7_pin18), .pin17(n7404_4_pin12),
    .pin16(n74244_7_pin16), .pin15(n7404_4_pin10), .pin14(n74244_7_pin14), .pin13(n7404_4_pin8),
    .pin12(n74244_7_pin12), .pin11(n7404_4_pin2));
  _7408 u_7408_9 (
    .pin1(n74244_1_pin16), .pin2(n74244_1_pin5), .pin3(n7408_9_pin3), .pin4(n74244_1_pin3),
    .pin5(n74244_1_pin18), .pin6(n7408_9_pin6), .pin13(n74244_1_pin9), .pin12(n74244_1_pin12),
    .pin11(n7408_9_pin11), .pin10(n74244_1_pin7), .pin9(n74244_1_pin14), .pin8(n7408_9_pin8));
  _7432 u_7432_3 (
    .pin1(n74244_1_pin16), .pin2(n74244_1_pin5), .pin3(n7432_3_pin3), .pin4(n74244_1_pin3),
    .pin5(n74244_1_pin18), .pin6(n7432_3_pin6), .pin13(n74244_1_pin9), .pin12(n74244_1_pin12),
    .pin11(n7432_3_pin11), .pin10(n74244_1_pin7), .pin9(n74244_1_pin14), .pin8(n7432_3_pin8));
  _7486 u_7486_1 (
    .pin1(n74244_1_pin16), .pin2(n74244_1_pin5), .pin3(n7486_1_pin3), .pin4(n74244_1_pin3),
    .pin5(n74244_1_pin18), .pin6(n7486_1_pin6), .pin13(n74244_1_pin9), .pin12(n74244_1_pin12),
    .pin11(n7486_1_pin11), .pin10(n74244_1_pin7), .pin9(n74244_1_pin14), .pin8(n7486_1_pin8));
  Pull_Resistor pull_resistor_14 (.node(n74244_7_pin16));
  Pull_Resistor pull_resistor_15 (.node(n74244_7_pin18));
  _74194 u_74194_1 (
    .pin1(n74161_1_pin1), .pin2(n74161_1_pin3), .pin3(n74244_1_pin12), .pin4(n74244_1_pin14),
    .pin5(n74244_1_pin16), .pin6(n74244_1_pin18), .pin7(n74161_1_pin3), .pin15(n74194_1_pin15),
    .pin14(n74194_1_pin14), .pin13(n74194_1_pin13), .pin12(n74194_1_pin12), .pin11(n7408_6_pin3),
    .pin10(n7432_2_pin11), .pin9(n7432_2_pin8));
  Pull_Resistor pull_resistor_16 (.node(n74244_7_pin3));
  Pull_Resistor pull_resistor_17 (.node(n74244_7_pin5));
  sub74HC191 sub74hc191_1 (
    .in_1(n74244_1_pin18), .in_2(n74244_1_pin16), .in_3(n74244_1_pin14), .in_4(n74244_1_pin12),
    .in_5(n7404_5_pin4), .in_6(n7432_2_pin10), .in_7(n74161_1_pin3), .in_8(n7408_7_pin6),
    .in_9(n74161_1_pin1), .in_10(n74161_1_pin3), .out_11(sub74hc191_1_out_11), .out_12(sub74hc191_1_out_12),
    .out_13(sub74hc191_1_out_13), .out_14(sub74hc191_1_out_14));  // open: out_15, out_16
  _7474 u_7474_2 (
    .pin1(n74161_1_pin1), .pin2(n7474_2_pin2), .pin3(n7474_2_pin3), .pin4(n74161_1_pin1),
    .pin5(n7474_2_pin5), .pin13(n74161_1_pin1), .pin12(n74161_1_pin3), .pin11(n74161_1_pin3),
    .pin10(n74161_1_pin1));  // open: pin6, pin9, pin8
  _74283 u_74283_1 (
    .pin1(n74283_1_pin1), .pin2(n74244_7_pin5), .pin3(n74244_7_pin16), .pin4(n74283_1_pin4),
    .pin5(n74244_7_pin18), .pin6(n74244_7_pin3), .pin7(n74283_1_pin7), .pin15(n74244_7_pin7),
    .pin14(n74244_7_pin14), .pin13(n74283_1_pin13), .pin12(n74244_7_pin12), .pin11(n74244_7_pin9),
    .pin10(n74283_1_pin10), .pin9(n7474_2_pin2));
  Pull_Resistor pull_resistor_18 (.node(n7474_2_pin3));
  sub74HC4066 sub74hc4066_2 (
    .in_1(n7474_2_pin5), .in_2(n7404_4_pin4), .in_3(n7408_6_pin12), .in_4(n7404_4_pin6),
    .in_5(n74161_1_pin1), .in_6(n7404_5_pin12), .in_9(n74161_1_pin1), .in_10(n74161_1_pin3),
    .out_11(n74283_1_pin7), .out_12(n7474_2_pin3), .out_13(n74283_1_pin7));  // open: in_7, in_8, out_14
  _74244 u_74244_9 (
    .pin1(n7404_4_pin5), .pin2(n74283_1_pin4), .pin3(n74244_5_pin3[0]), .pin4(n74283_1_pin1),
    .pin5(n74244_5_pin3[1]), .pin6(n74283_1_pin13), .pin7(n74244_5_pin3[2]), .pin8(n74283_1_pin10),
    .pin9(n74244_5_pin3[3]), .pin19(n7408_3_pin13), .pin18(n74244_5_pin3[0]), .pin17(n7408_9_pin6),
    .pin16(n74244_5_pin3[1]), .pin15(n7408_9_pin3), .pin14(n74244_5_pin3[2]), .pin13(n7408_9_pin8),
    .pin12(n74244_5_pin3[3]), .pin11(n7408_9_pin11));
  _74244 u_74244_10 (
    .pin1(n7408_3_pin12), .pin2(n7432_3_pin6), .pin3(n74244_5_pin3[0]), .pin4(n7432_3_pin3),
    .pin5(n74244_5_pin3[1]), .pin6(n7432_3_pin8), .pin7(n74244_5_pin3[2]), .pin8(n7432_3_pin11),
    .pin9(n74244_5_pin3[3]), .pin19(n7408_3_pin10), .pin18(n74244_5_pin3[0]), .pin17(n7486_1_pin6),
    .pin16(n74244_5_pin3[1]), .pin15(n7486_1_pin3), .pin14(n74244_5_pin3[2]), .pin13(n7486_1_pin8),
    .pin12(n74244_5_pin3[3]), .pin11(n7486_1_pin11));
  Pull_Resistor pull_resistor_19 (.node(n74283_1_pin7));
  _74244 u_74244_11 (
    .pin1(n7408_3_pin9), .pin2(sub74hc191_1_out_11), .pin3(n74244_5_pin3[0]), .pin4(sub74hc191_1_out_12),
    .pin5(n74244_5_pin3[1]), .pin6(sub74hc191_1_out_13), .pin7(n74244_5_pin3[2]), .pin8(sub74hc191_1_out_14),
    .pin9(n74244_5_pin3[3]), .pin19(n7408_4_pin2), .pin18(n74244_5_pin3[0]), .pin17(n74194_1_pin12),
    .pin16(n74244_5_pin3[1]), .pin15(n74194_1_pin13), .pin14(n74244_5_pin3[2]), .pin13(n74194_1_pin14),
    .pin12(n74244_5_pin3[3]), .pin11(n74194_1_pin15));
  Pull_Resistor pull_resistor_20 (.node(n74244_5_pin3[0]));
  Pull_Resistor pull_resistor_21 (.node(n74244_5_pin3[1]));
  Pull_Resistor pull_resistor_22 (.node(n74244_5_pin3[2]));
  Pull_Resistor pull_resistor_23 (.node(n74244_5_pin3[3]));
  // also tied to GND on the sheet: n74161_1_pin3
  // also tied to VCC on the sheet: n74161_1_pin1

  // Notes on the sheet:
  //   JZ
  //   ST
  //   1х3
  //   102
  //   014
  //   104
  //   1х3
  //   contents of rom_1 (hex, n*v repeats v):
  //   0 b0 c b4 5 b8 3 cd 61 72 82 a1 a0 20 50 1c 50 b0 d 31 42 51 91 90 20 51 23 52
endmodule
