// Logisim project Registers.circ as structural Verilog: 1 circuit, main circuit main
module main (
);

  wire clock_1_out, controlled_buffer_6_out, controlled_buffer_11_out, controlled_buffer_16_out,
       controlled_buffer_21_out, controlled_buffer_25_out, controlled_buffer_26_out,
       controlled_buffer_27_out, controlled_buffer_28_out, controlled_buffer_29_out,
       controlled_buffer_30_out, controlled_buffer_31_out, controlled_buffer_32_out,
       controlled_buffer_65_out, d_ff_1_q, d_ff_2_q, d_ff_3_q, d_ff_4_q, d_ff_5_q, d_ff_6_q, d_ff_7_q,
       d_ff_8_q, d_ff_9_q, d_ff_10_q, d_ff_11_q, d_ff_12_q, d_ff_13_q, d_ff_14_q, d_ff_15_q, d_ff_16_q,
       decoder_1_out0, decoder_1_out1, decoder_1_out2, decoder_1_out3, decoder_2_out0, decoder_2_out1,
       decoder_2_out2, decoder_2_out3, decoder_3_out0, decoder_3_out1, decoder_3_out2, decoder_3_out3,
       decoder_4_out0, decoder_4_out1, decoder_4_out2, decoder_4_out3, dipswitch_1_sw1, dipswitch_1_sw2,
       dipswitch_1_sw3, dipswitch_1_sw4, nor_1_out, nor_2_out, nor_3_out, nor_4_out, pull_resistor_1_node,
       pull_resistor_2_node, pull_resistor_3_node, pull_resistor_4_node, pull_resistor_5_node,
       pull_resistor_6_node, pull_resistor_7_node, pull_resistor_8_node, pull_resistor_9_node,
       pull_resistor_10_node, pull_resistor_11_node, pull_resistor_12_node, pull_resistor_13_node,
       pull_resistor_14_node, pull_resistor_15_node, pull_resistor_16_node, pull_resistor_17_node,
       pull_resistor_18_node, pull_resistor_19_node, pull_resistor_20_node, pull_resistor_25_node,
       pull_resistor_26_node, pull_resistor_27_node, pull_resistor_28_node, pull_resistor_29_node,
       pull_resistor_30_node, pull_resistor_31_node, pull_resistor_32_node, pull_resistor_33_node,
       pull_resistor_34_node, pull_resistor_35_node, pull_resistor_45_node, pull_resistor_46_node,
       pull_resistor_48_node, pull_resistor_49_node, switch_4_p1;
  wire [1:0] dipswitch_2_sw1, dipswitch_2_sw3, dipswitch_2_sw5, dipswitch_2_sw7;

  DipSwitch dipswitch_1 (
    .sw1(dipswitch_1_sw1), .sw2(dipswitch_1_sw2), .sw3(dipswitch_1_sw3), .sw4(dipswitch_1_sw4));  // open: sw5, sw6, sw7, sw8
  Decoder #(.select(2)) decoder_1 (
    .out0(decoder_1_out0), .out1(decoder_1_out1), .out2(decoder_1_out2), .out3(decoder_1_out3),
    .sel(dipswitch_2_sw1));  // open: en
  Pull_Resistor pull_resistor_1 (.node(pull_resistor_1_node));
  Pull_Resistor pull_resistor_2 (.node(pull_resistor_2_node));
  assign pull_resistor_2_node = pull_resistor_35_node ? decoder_1_out1 : 1'bz;  // Controlled_Buffer controlled_buffer_1
  assign pull_resistor_1_node = pull_resistor_35_node ? decoder_1_out0 : 1'bz;  // Controlled_Buffer controlled_buffer_2
  Clock clock_1 (.out(clock_1_out));
  Pull_Resistor pull_resistor_3 (.node(pull_resistor_3_node));
  Pull_Resistor pull_resistor_4 (.node(pull_resistor_4_node));
  assign pull_resistor_4_node = pull_resistor_35_node ? decoder_1_out3 : 1'bz;  // Controlled_Buffer controlled_buffer_3
  assign pull_resistor_3_node = pull_resistor_35_node ? decoder_1_out2 : 1'bz;  // Controlled_Buffer controlled_buffer_4
  DipSwitch dipswitch_2 (
    .sw1(dipswitch_2_sw1[0]), .sw2(dipswitch_2_sw1[1]), .sw3(dipswitch_2_sw3[0]), .sw4(dipswitch_2_sw3[1]),
    .sw5(dipswitch_2_sw5[0]), .sw6(dipswitch_2_sw5[1]), .sw7(dipswitch_2_sw7[0]), .sw8(dipswitch_2_sw7[1]));
  Pull_Resistor pull_resistor_5 (.node(pull_resistor_5_node));
  assign pull_resistor_5_node = pull_resistor_1_node ? dipswitch_1_sw1 : 1'bz;  // Controlled_Buffer controlled_buffer_5
  assign controlled_buffer_6_out = pull_resistor_1_node ? clock_1_out : 1'bz;  // Controlled_Buffer controlled_buffer_6
  Pull_Resistor pull_resistor_6 (.node(pull_resistor_6_node));
  assign pull_resistor_6_node = pull_resistor_1_node ? dipswitch_1_sw2 : 1'bz;  // Controlled_Buffer controlled_buffer_7
  Pull_Resistor pull_resistor_7 (.node(pull_resistor_7_node));
  assign pull_resistor_7_node = pull_resistor_1_node ? dipswitch_1_sw3 : 1'bz;  // Controlled_Buffer controlled_buffer_8
  Pull_Resistor pull_resistor_8 (.node(pull_resistor_8_node));
  assign pull_resistor_8_node = pull_resistor_1_node ? dipswitch_1_sw4 : 1'bz;  // Controlled_Buffer controlled_buffer_9
  Pull_Resistor pull_resistor_9 (.node(pull_resistor_9_node));
  assign pull_resistor_9_node = pull_resistor_2_node ? dipswitch_1_sw1 : 1'bz;  // Controlled_Buffer controlled_buffer_10
  assign controlled_buffer_11_out = pull_resistor_2_node ? clock_1_out : 1'bz;  // Controlled_Buffer controlled_buffer_11
  Pull_Resistor pull_resistor_10 (.node(pull_resistor_10_node));
  assign pull_resistor_10_node = pull_resistor_2_node ? dipswitch_1_sw2 : 1'bz;  // Controlled_Buffer controlled_buffer_12
  Pull_Resistor pull_resistor_11 (.node(pull_resistor_11_node));
  assign pull_resistor_11_node = pull_resistor_2_node ? dipswitch_1_sw3 : 1'bz;  // Controlled_Buffer controlled_buffer_13
  Pull_Resistor pull_resistor_12 (.node(pull_resistor_12_node));
  assign pull_resistor_12_node = pull_resistor_2_node ? dipswitch_1_sw4 : 1'bz;  // Controlled_Buffer controlled_buffer_14
  Pull_Resistor pull_resistor_13 (.node(pull_resistor_13_node));
  assign pull_resistor_13_node = pull_resistor_3_node ? dipswitch_1_sw1 : 1'bz;  // Controlled_Buffer controlled_buffer_15
  assign controlled_buffer_16_out = pull_resistor_3_node ? clock_1_out : 1'bz;  // Controlled_Buffer controlled_buffer_16
  Pull_Resistor pull_resistor_14 (.node(pull_resistor_14_node));
  assign pull_resistor_14_node = pull_resistor_3_node ? dipswitch_1_sw2 : 1'bz;  // Controlled_Buffer controlled_buffer_17
  Pull_Resistor pull_resistor_15 (.node(pull_resistor_15_node));
  assign pull_resistor_15_node = pull_resistor_3_node ? dipswitch_1_sw3 : 1'bz;  // Controlled_Buffer controlled_buffer_18
  Pull_Resistor pull_resistor_16 (.node(pull_resistor_16_node));
  assign pull_resistor_16_node = pull_resistor_3_node ? dipswitch_1_sw4 : 1'bz;  // Controlled_Buffer controlled_buffer_19
  Pull_Resistor pull_resistor_17 (.node(pull_resistor_17_node));
  assign pull_resistor_17_node = pull_resistor_4_node ? dipswitch_1_sw1 : 1'bz;  // Controlled_Buffer controlled_buffer_20
  assign controlled_buffer_21_out = pull_resistor_4_node ? clock_1_out : 1'bz;  // Controlled_Buffer controlled_buffer_21
  Pull_Resistor pull_resistor_18 (.node(pull_resistor_18_node));
  assign pull_resistor_18_node = pull_resistor_4_node ? dipswitch_1_sw2 : 1'bz;  // Controlled_Buffer controlled_buffer_22
  Pull_Resistor pull_resistor_19 (.node(pull_resistor_19_node));
  assign pull_resistor_19_node = pull_resistor_4_node ? dipswitch_1_sw3 : 1'bz;  // Controlled_Buffer controlled_buffer_23
  Pull_Resistor pull_resistor_20 (.node(pull_resistor_20_node));
  assign pull_resistor_20_node = pull_resistor_4_node ? dipswitch_1_sw4 : 1'bz;  // Controlled_Buffer controlled_buffer_24
  D_Flip_Flop d_ff_1 (
    .D(pull_resistor_5_node), .clk(controlled_buffer_6_out), .Q(d_ff_1_q));  // open: Qn, preset, reset
  D_Flip_Flop d_ff_2 (
    .D(pull_resistor_6_node), .clk(controlled_buffer_6_out), .Q(d_ff_2_q));  // open: Qn, preset, reset
  D_Flip_Flop d_ff_3 (
    .D(pull_resistor_7_node), .clk(controlled_buffer_6_out), .Q(d_ff_3_q));  // open: Qn, preset, reset
  D_Flip_Flop d_ff_4 (
    .D(pull_resistor_8_node), .clk(controlled_buffer_6_out), .Q(d_ff_4_q));  // open: Qn, preset, reset
  Pull_Resistor pull_resistor_21 (.node(controlled_buffer_6_out));
  D_Flip_Flop d_ff_5 (
    .D(pull_resistor_9_node), .clk(controlled_buffer_11_out), .Q(d_ff_5_q));  // open: Qn, preset, reset
  D_Flip_Flop d_ff_6 (
    .D(pull_resistor_10_node), .clk(controlled_buffer_11_out), .Q(d_ff_6_q));  // open: Qn, preset, reset
  D_Flip_Flop d_ff_7 (
    .D(pull_resistor_11_node), .clk(controlled_buffer_11_out), .Q(d_ff_7_q));  // open: Qn, preset, reset
  D_Flip_Flop d_ff_8 (
    .D(pull_resistor_12_node), .clk(controlled_buffer_11_out), .Q(d_ff_8_q));  // open: Qn, preset, reset
  Pull_Resistor pull_resistor_22 (.node(controlled_buffer_11_out));
  D_Flip_Flop d_ff_9 (
    .D(pull_resistor_13_node), .clk(controlled_buffer_16_out), .Q(d_ff_9_q));  // open: Qn, preset, reset
  D_Flip_Flop d_ff_10 (
    .D(pull_resistor_14_node), .clk(controlled_buffer_16_out), .Q(d_ff_10_q));  // open: Qn, preset, reset
  D_Flip_Flop d_ff_11 (
    .D(pull_resistor_15_node), .clk(controlled_buffer_16_out), .Q(d_ff_11_q));  // open: Qn, preset, reset
  D_Flip_Flop d_ff_12 (
    .D(pull_resistor_16_node), .clk(controlled_buffer_16_out), .Q(d_ff_12_q));  // open: Qn, preset, reset
  Pull_Resistor pull_resistor_23 (.node(controlled_buffer_16_out));
  D_Flip_Flop d_ff_13 (
    .D(pull_resistor_17_node), .clk(controlled_buffer_21_out), .Q(d_ff_13_q));  // open: Qn, preset, reset
  D_Flip_Flop d_ff_14 (
    .D(pull_resistor_18_node), .clk(controlled_buffer_21_out), .Q(d_ff_14_q));  // open: Qn, preset, reset
  D_Flip_Flop d_ff_15 (
    .D(pull_resistor_19_node), .clk(controlled_buffer_21_out), .Q(d_ff_15_q));  // open: Qn, preset, reset
  D_Flip_Flop d_ff_16 (
    .D(pull_resistor_20_node), .clk(controlled_buffer_21_out), .Q(d_ff_16_q));  // open: Qn, preset, reset
  Pull_Resistor pull_resistor_24 (.node(controlled_buffer_21_out));
  assign controlled_buffer_25_out = pull_resistor_30_node ? d_ff_1_q : 1'bz;  // Controlled_Buffer controlled_buffer_25
  assign controlled_buffer_26_out = pull_resistor_32_node ? d_ff_1_q : 1'bz;  // Controlled_Buffer controlled_buffer_26
  assign controlled_buffer_27_out = pull_resistor_30_node ? d_ff_2_q : 1'bz;  // Controlled_Buffer controlled_buffer_27
  assign controlled_buffer_28_out = pull_resistor_32_node ? d_ff_2_q : 1'bz;  // Controlled_Buffer controlled_buffer_28
  assign controlled_buffer_29_out = pull_resistor_30_node ? d_ff_3_q : 1'bz;  // Controlled_Buffer controlled_buffer_29
  assign controlled_buffer_30_out = pull_resistor_32_node ? d_ff_3_q : 1'bz;  // Controlled_Buffer controlled_buffer_30
  assign controlled_buffer_31_out = pull_resistor_30_node ? d_ff_4_q : 1'bz;  // Controlled_Buffer controlled_buffer_31
  assign controlled_buffer_32_out = pull_resistor_32_node ? d_ff_4_q : 1'bz;  // Controlled_Buffer controlled_buffer_32
  assign controlled_buffer_25_out = pull_resistor_28_node ? d_ff_5_q : 1'bz;  // Controlled_Buffer controlled_buffer_33
  assign controlled_buffer_26_out = pull_resistor_31_node ? d_ff_5_q : 1'bz;  // Controlled_Buffer controlled_buffer_34
  assign controlled_buffer_27_out = pull_resistor_28_node ? d_ff_6_q : 1'bz;  // Controlled_Buffer controlled_buffer_35
  assign controlled_buffer_28_out = pull_resistor_31_node ? d_ff_6_q : 1'bz;  // Controlled_Buffer controlled_buffer_36
  assign controlled_buffer_29_out = pull_resistor_28_node ? d_ff_7_q : 1'bz;  // Controlled_Buffer controlled_buffer_37
  assign controlled_buffer_30_out = pull_resistor_31_node ? d_ff_7_q : 1'bz;  // Controlled_Buffer controlled_buffer_38
  assign controlled_buffer_31_out = pull_resistor_28_node ? d_ff_8_q : 1'bz;  // Controlled_Buffer controlled_buffer_39
  assign controlled_buffer_32_out = pull_resistor_31_node ? d_ff_8_q : 1'bz;  // Controlled_Buffer controlled_buffer_40
  assign controlled_buffer_25_out = pull_resistor_26_node ? d_ff_9_q : 1'bz;  // Controlled_Buffer controlled_buffer_41
  assign controlled_buffer_26_out = pull_resistor_29_node ? d_ff_9_q : 1'bz;  // Controlled_Buffer controlled_buffer_42
  assign controlled_buffer_27_out = pull_resistor_26_node ? d_ff_10_q : 1'bz;  // Controlled_Buffer controlled_buffer_43
  assign controlled_buffer_28_out = pull_resistor_29_node ? d_ff_10_q : 1'bz;  // Controlled_Buffer controlled_buffer_44
  assign controlled_buffer_29_out = pull_resistor_26_node ? d_ff_11_q : 1'bz;  // Controlled_Buffer controlled_buffer_45
  assign controlled_buffer_30_out = pull_resistor_29_node ? d_ff_11_q : 1'bz;  // Controlled_Buffer controlled_buffer_46
  assign controlled_buffer_31_out = pull_resistor_26_node ? d_ff_12_q : 1'bz;  // Controlled_Buffer controlled_buffer_47
  assign controlled_buffer_32_out = pull_resistor_29_node ? d_ff_12_q : 1'bz;  // Controlled_Buffer controlled_buffer_48
  assign controlled_buffer_25_out = pull_resistor_25_node ? d_ff_13_q : 1'bz;  // Controlled_Buffer controlled_buffer_49
  assign controlled_buffer_26_out = pull_resistor_27_node ? d_ff_13_q : 1'bz;  // Controlled_Buffer controlled_buffer_50
  assign controlled_buffer_27_out = pull_resistor_25_node ? d_ff_14_q : 1'bz;  // Controlled_Buffer controlled_buffer_51
  assign controlled_buffer_28_out = pull_resistor_27_node ? d_ff_14_q : 1'bz;  // Controlled_Buffer controlled_buffer_52
  assign controlled_buffer_29_out = pull_resistor_25_node ? d_ff_15_q : 1'bz;  // Controlled_Buffer controlled_buffer_53
  assign controlled_buffer_30_out = pull_resistor_27_node ? d_ff_15_q : 1'bz;  // Controlled_Buffer controlled_buffer_54
  assign controlled_buffer_31_out = pull_resistor_25_node ? d_ff_16_q : 1'bz;  // Controlled_Buffer controlled_buffer_55
  assign controlled_buffer_32_out = pull_resistor_27_node ? d_ff_16_q : 1'bz;  // Controlled_Buffer controlled_buffer_56
  Pull_Resistor pull_resistor_25 (.node(pull_resistor_25_node));
  assign pull_resistor_25_node = pull_resistor_33_node ? decoder_2_out3 : 1'bz;  // Controlled_Buffer controlled_buffer_57
  Decoder #(.select(2)) decoder_2 (
    .out0(decoder_2_out0), .out1(decoder_2_out1), .out2(decoder_2_out2), .out3(decoder_2_out3),
    .sel(dipswitch_2_sw3));  // open: en
  Decoder #(.select(2)) decoder_3 (
    .out0(decoder_3_out0), .out1(decoder_3_out1), .out2(decoder_3_out2), .out3(decoder_3_out3),
    .sel(dipswitch_2_sw5));  // open: en
  Pull_Resistor pull_resistor_26 (.node(pull_resistor_26_node));
  assign pull_resistor_26_node = pull_resistor_33_node ? decoder_2_out2 : 1'bz;  // Controlled_Buffer controlled_buffer_58
  Pull_Resistor pull_resistor_27 (.node(pull_resistor_27_node));
  assign pull_resistor_27_node = pull_resistor_34_node ? decoder_3_out3 : 1'bz;  // Controlled_Buffer controlled_buffer_59
  Pull_Resistor pull_resistor_28 (.node(pull_resistor_28_node));
  assign pull_resistor_28_node = pull_resistor_33_node ? decoder_2_out1 : 1'bz;  // Controlled_Buffer controlled_buffer_60
  Pull_Resistor pull_resistor_29 (.node(pull_resistor_29_node));
  assign pull_resistor_29_node = pull_resistor_34_node ? decoder_3_out2 : 1'bz;  // Controlled_Buffer controlled_buffer_61
  Pull_Resistor pull_resistor_30 (.node(pull_resistor_30_node));
  assign pull_resistor_30_node = pull_resistor_33_node ? decoder_2_out0 : 1'bz;  // Controlled_Buffer controlled_buffer_62
  Pull_Resistor pull_resistor_31 (.node(pull_resistor_31_node));
  assign pull_resistor_31_node = pull_resistor_34_node ? decoder_3_out1 : 1'bz;  // Controlled_Buffer controlled_buffer_63
  Pull_Resistor pull_resistor_32 (.node(pull_resistor_32_node));
  assign pull_resistor_32_node = pull_resistor_34_node ? decoder_3_out0 : 1'bz;  // Controlled_Buffer controlled_buffer_64
  Pull_Resistor pull_resistor_33 (.node(pull_resistor_33_node));
  Pull_Resistor pull_resistor_34 (.node(pull_resistor_34_node));
  Pull_Resistor pull_resistor_35 (.node(pull_resistor_35_node));
  // Switch switch_1: pin names not known; wires that end beside it: pull_resistor_35_node, 1'b1
  // Switch switch_2: pin names not known; wires that end beside it: pull_resistor_34_node, 1'b1
  Pull_Resistor pull_resistor_36 (.node(controlled_buffer_25_out));
  Pull_Resistor pull_resistor_37 (.node(controlled_buffer_27_out));
  Pull_Resistor pull_resistor_38 (.node(controlled_buffer_29_out));
  Pull_Resistor pull_resistor_39 (.node(controlled_buffer_31_out));
  Pull_Resistor pull_resistor_40 (.node(controlled_buffer_26_out));
  Pull_Resistor pull_resistor_41 (.node(controlled_buffer_28_out));
  Pull_Resistor pull_resistor_42 (.node(controlled_buffer_30_out));
  Pull_Resistor pull_resistor_43 (.node(controlled_buffer_32_out));
  // Switch switch_3: pin names not known; wires that end beside it: pull_resistor_33_node, 1'b1
  // Switch switch_4: pin names not known; wires that end beside it: switch_4_p1, 1'b1
  Pull_Resistor pull_resistor_44 (.node(switch_4_p1));
  Decoder #(.select(2)) decoder_4 (
    .out0(decoder_4_out0), .out1(decoder_4_out1), .out2(decoder_4_out2), .out3(decoder_4_out3),
    .sel(dipswitch_2_sw7));  // open: en
  LED led_1 (.in(controlled_buffer_25_out));
  LED led_2 (.in(controlled_buffer_27_out));
  LED led_3 (.in(controlled_buffer_29_out));
  LED led_4 (.in(controlled_buffer_31_out));
  LED led_5 (.in(controlled_buffer_26_out));
  LED led_6 (.in(controlled_buffer_28_out));
  LED led_7 (.in(controlled_buffer_30_out));
  LED led_8 (.in(controlled_buffer_32_out));
  nor nor_1 (nor_1_out, d_ff_1_q, d_ff_2_q, d_ff_3_q, d_ff_4_q);
  assign controlled_buffer_65_out = pull_resistor_46_node ? nor_1_out : 1'bz;  // Controlled_Buffer controlled_buffer_65
  nor nor_2 (nor_2_out, d_ff_5_q, d_ff_6_q, d_ff_7_q, d_ff_8_q);
  assign controlled_buffer_65_out = pull_resistor_45_node ? nor_2_out : 1'bz;  // Controlled_Buffer controlled_buffer_66
  nor nor_3 (nor_3_out, d_ff_9_q, d_ff_10_q, d_ff_11_q, d_ff_12_q);
  nor nor_4 (nor_4_out, d_ff_13_q, d_ff_14_q, d_ff_15_q, d_ff_16_q);
  Pull_Resistor pull_resistor_45 (.node(pull_resistor_45_node));
  Pull_Resistor pull_resistor_46 (.node(pull_resistor_46_node));
  assign pull_resistor_45_node = switch_4_p1 ? decoder_4_out1 : 1'bz;  // Controlled_Buffer controlled_buffer_67
  assign pull_resistor_46_node = switch_4_p1 ? decoder_4_out0 : 1'bz;  // Controlled_Buffer controlled_buffer_68
  assign controlled_buffer_65_out = pull_resistor_49_node ? nor_3_out : 1'bz;  // Controlled_Buffer controlled_buffer_69
  Pull_Resistor pull_resistor_47 (.node(controlled_buffer_65_out));
  assign controlled_buffer_65_out = pull_resistor_48_node ? nor_4_out : 1'bz;  // Controlled_Buffer controlled_buffer_70
  Pull_Resistor pull_resistor_48 (.node(pull_resistor_48_node));
  Pull_Resistor pull_resistor_49 (.node(pull_resistor_49_node));
  assign pull_resistor_48_node = switch_4_p1 ? decoder_4_out3 : 1'bz;  // Controlled_Buffer controlled_buffer_71
  assign pull_resistor_49_node = switch_4_p1 ? decoder_4_out2 : 1'bz;  // Controlled_Buffer controlled_buffer_72
  LED led_9 (.in(controlled_buffer_65_out));
endmodule
